// Logisim project MIPS CPU设计实验.circ as structural Verilog: 5 circuits, main circuit 多周期MIPS(微程序)
module \多周期MIPS_微程序  (
);

  wire AluSrcA, and_1_out, and_2_out, Beq, Bne, CLK, IorD, MemRead, MemWrite, mips_alu_1_equal, or_1_out,
       PcSrc, RST, \多周期微程序控制器_1_irwrite , \多周期微程序控制器_1_memtoreg , \多周期微程序控制器_1_pcwrite ,
       \多周期微程序控制器_1_regdst , \多周期微程序控制器_1_regwrite ;
  wire [1:0] AluSrcB;
  wire [3:0] AluOP, \多周期微程序控制器_1_addr ;
  wire [4:0] multiplexer_2_out;
  wire [31:0] A_q, B_q, bit_extender_1_out, C_q, DR_q, IR_q, mips_alu_1_result, mips_regifile_1_r1,
       mips_regifile_1_r2, multiplexer_1_out, multiplexer_3_out, multiplexer_4_out, multiplexer_5_out,
       multiplexer_6_out, PC_q, ram_1_data, shifter_1_out;

  Register #(.width(32), .trigger("rising"), .Select("low")) PC (
    .D(multiplexer_6_out), .en(or_1_out), .Q(PC_q), .clk(CLK), .clr(RST));
  Button button_1 (.out(RST));
  Clock #(.highDuration(1), .lowDuration(1)) clock_1 (.out(CLK));
  Multiplexer #(.select(1), .width(32), .disabled("Z"), .enable("false")) multiplexer_1 (
    .in0(PC_q), .in1(C_q), .out(multiplexer_1_out), .sel(IorD));
  RAM #(.addrWidth(10), .dataWidth(32), .bus("separate"), .Select("high")) ram_1 (
    .addr(multiplexer_1_out[11:2]), .din(B_q), .data(ram_1_data), .str(MemWrite), .clk(CLK), .ld(MemRead));  // open: sel, clr
  Register #(.width(32), .trigger("rising"), .Select("low")) IR (
    .D(ram_1_data), .en(\多周期微程序控制器_1_irwrite ), .Q(IR_q), .clk(CLK), .clr(RST));
  Register #(.width(32), .trigger("rising"), .Select("low")) DR (
    .D(ram_1_data), .Q(DR_q), .clk(CLK), .clr(RST));  // open: en
  // Probe on \多周期微程序控制器_1_addr 
  \多周期微程序控制器  \u_多周期微程序控制器_1  (
    .PcWrite(\多周期微程序控制器_1_pcwrite ), .Beq(Beq), .PCsrc(PcSrc), .AluSrcB(AluSrcB), .AluSrcA(AluSrcA),
    .RegWrite(\多周期微程序控制器_1_regwrite ), .MemToReg(\多周期微程序控制器_1_memtoreg ), .RegDst(\多周期微程序控制器_1_regdst ),
    .OP(IR_q[31:26]), .IorD(IorD), .MemWrite(MemWrite), .MemRead(MemRead), .IrWrite(\多周期微程序控制器_1_irwrite ),
    .Bne(Bne), .CLK(CLK), .Addr(\多周期微程序控制器_1_addr ), .RST(RST), .ALU_OP(AluOP), .in_4(IR_q[5:0]));
  Multiplexer #(.select(1), .width(5), .disabled("Z"), .enable("false")) multiplexer_2 (
    .in0(IR_q[20:16]), .in1(IR_q[15:11]), .out(multiplexer_2_out), .sel(\多周期微程序控制器_1_regdst ));
  Multiplexer #(.select(1), .width(32), .disabled("Z"), .enable("false")) multiplexer_3 (
    .in0(C_q), .in1(DR_q), .out(multiplexer_3_out), .sel(\多周期微程序控制器_1_memtoreg ));
  assign bit_extender_1_out = {{16{IR_q[15]}}, IR_q[15:0]};  // Bit_Extender bit_extender_1
  MIPS_Regifile mips_regifile_1 (
    .Din(multiplexer_3_out), .Clk(CLK), .R1(mips_regifile_1_r1), .R2(mips_regifile_1_r2),
    .WE(\多周期微程序控制器_1_regwrite ), .W_num(multiplexer_2_out), .R1_num(IR_q[25:21]), .R2_num(IR_q[20:16]));
  Register #(.width(32), .trigger("rising"), .Select("low")) A (
    .D(mips_regifile_1_r1), .Q(A_q), .clk(CLK), .clr(RST));  // open: en
  Register #(.width(32), .trigger("rising"), .Select("low")) B (
    .D(mips_regifile_1_r2), .Q(B_q), .clk(CLK), .clr(RST));  // open: en
  Multiplexer #(.select(1), .width(32), .disabled("Z"), .enable("false")) multiplexer_4 (
    .in0(PC_q), .in1(A_q), .out(multiplexer_4_out), .sel(AluSrcA));
  Shifter #(.width(32), .shift("ll")) shifter_1 (.in(bit_extender_1_out), .\dist (5'b00010), .out(shifter_1_out));
  Multiplexer #(.select(2), .width(32), .disabled("Z"), .enable("false")) multiplexer_5 (
    .in0(B_q), .in1(32'h4), .in2(bit_extender_1_out), .in3(shifter_1_out), .out(multiplexer_5_out),
    .sel(AluSrcB));
  MIPS_ALU mips_alu_1 (
    .X(multiplexer_4_out), .Y(multiplexer_5_out), .AluOP(AluOP), .Equal(mips_alu_1_equal),
    .Result(mips_alu_1_result));  // open: Result_2
  Register #(.width(32), .trigger("rising"), .Select("low")) C (
    .D(mips_alu_1_result), .Q(C_q), .clk(CLK), .clr(RST));  // open: en
  or or_1 (or_1_out, \多周期微程序控制器_1_pcwrite , and_1_out, and_2_out);
  and and_1 (and_1_out, Beq, mips_alu_1_equal);
  and and_2 (and_2_out, Bne, ~mips_alu_1_equal);  // AND_Gate
  Multiplexer #(.select(1), .width(32), .disabled("Z"), .enable("false")) multiplexer_6 (
    .in0(mips_alu_1_result), .in1(C_q), .out(multiplexer_6_out), .sel(PcSrc));

  // Notes on the sheet:
  //   程序计数器
  //   IorD
  //   存储器
  //   IRWrite
  //   指令字
  //   IorD
  //   MemWrite
  //   MemRead
  //   IRWrite
  //   OP
  //   Func
  //   RegDst
  //   rs
  //   rt
  //   rd
  //   Imm16
  //   PcWrite
  //   Beq
  //   Bne
  //   PcSrc
  //   AluOP
  //   AluSrcB
  //   AluSrcA
  //   RegWrite
  //   MemToReg
  //   寄存器堆
  //   PcEnable
  //   运算器
endmodule

// 微程序控制器
module \多周期微程序控制器  (
  input  CLK,
  input  RST,
  input  [5:0] OP,
  input  [5:0] in_4,
  output Bne,
  output Beq,
  output MemRead,
  output MemWrite,
  output RegWrite,
  output PcWrite,
  output [3:0] Addr,
  output IrWrite,
  output RegDst,
  output MemToReg,
  output AluSrcA,
  output [1:0] AluSrcB,
  output PCsrc,
  output IorD,
  output [3:0] ALU_OP
);

  wire ADD, ADDI, AND, BEQ_t, BNE_t, comparator_6_eq, comparator_7_eq, comparator_8_eq, comparator_9_eq,
       comparator_10_eq, comparator_11_eq, comparator_12_eq, comparator_13_eq, comparator_14_eq,
       comparator_15_eq, comparator_16_eq, comparator_17_eq, comparator_18_eq, comparator_19_eq,
       comparator_20_eq, comparator_21_eq, JR, LW, NOR, OR, or_2_out, or_3_out, or_4_out, P, R_TYPE, SLL,
       SLLV, SLT, SRA, SRAV, SRL, SRLV, SUB, SW, SysCall, XOR;
  wire [1:0] ALU_Control;
  wire [3:0] multiplexer_1_out, multiplexer_2_out, multiplexer_3_out, multiplexer_4_out, multiplexer_5_out,
       multiplexer_6_out, multiplexer_7_out, multiplexer_8_out, multiplexer_9_out, multiplexer_10_out,
       multiplexer_11_out, rom_1_data, \微程序地址转移逻辑_1_s0 ;

  Comparator #(.width(6), .mode("twosComplement")) comparator_1 (.a(OP), .b(6'b100011), .eq(LW));  // open: gt, lt
  Comparator #(.width(6), .mode("twosComplement")) comparator_2 (.a(OP), .b(6'b101011), .eq(SW));  // open: gt, lt
  Comparator #(.width(6), .mode("twosComplement")) comparator_3 (.a(OP), .b(6'b000100), .eq(BEQ_t));  // open: gt, lt
  Comparator #(.width(6), .mode("twosComplement")) comparator_4 (.a(OP), .b(6'b000101), .eq(BNE_t));  // open: gt, lt
  Comparator #(.width(6), .mode("twosComplement")) comparator_5 (.a(OP), .b(6'b001000), .eq(ADDI));  // open: gt, lt
  Comparator #(.width(6), .mode("twosComplement")) comparator_6 (
    .a(OP), .b({6{1'b0}}), .eq(comparator_6_eq));  // open: gt, lt
  \微程序地址转移逻辑  \u_微程序地址转移逻辑_1  (
    .R_Type(R_TYPE), .S3(\微程序地址转移逻辑_1_s0 [3]), .ADDI(ADDI), .S2(\微程序地址转移逻辑_1_s0 [2]), .LW(LW),
    .S1(\微程序地址转移逻辑_1_s0 [1]), .SW(SW), .S0(\微程序地址转移逻辑_1_s0 [0]), .BEQ(BEQ_t), .BNE(BNE_t), .SYSCALL(SysCall));
  Comparator #(.width(6), .mode("twosComplement")) comparator_7 (
    .a(in_4), .b(6'b001000), .eq(comparator_7_eq));  // open: gt, lt
  Comparator #(.width(6), .mode("twosComplement")) comparator_8 (
    .a(in_4), .b(6'b000111), .eq(comparator_8_eq));  // open: gt, lt
  Comparator #(.width(6), .mode("twosComplement")) comparator_9 (
    .a(in_4), .b(6'b000110), .eq(comparator_9_eq));  // open: gt, lt
  Comparator #(.width(6), .mode("twosComplement")) comparator_10 (
    .a(in_4), .b(6'b000100), .eq(comparator_10_eq));  // open: gt, lt
  Comparator #(.width(6), .mode("twosComplement")) comparator_11 (
    .a(in_4), .b({6{1'b0}}), .eq(comparator_11_eq));  // open: gt, lt
  Comparator #(.width(6), .mode("twosComplement")) comparator_12 (
    .a(in_4), .b(6'b000010), .eq(comparator_12_eq));  // open: gt, lt
  Comparator #(.width(6), .mode("twosComplement")) comparator_13 (
    .a(in_4), .b(6'b000011), .eq(comparator_13_eq));  // open: gt, lt
  Comparator #(.width(6), .mode("twosComplement")) comparator_14 (
    .a(in_4), .b(6'b100111), .eq(comparator_14_eq));  // open: gt, lt
  Comparator #(.width(6), .mode("twosComplement")) comparator_15 (
    .a(in_4), .b(6'b100110), .eq(comparator_15_eq));  // open: gt, lt
  Comparator #(.width(6), .mode("twosComplement")) comparator_16 (
    .a(in_4), .b(6'b100101), .eq(comparator_16_eq));  // open: gt, lt
  Comparator #(.width(6), .mode("twosComplement")) comparator_17 (
    .a(in_4), .b(6'b100100), .eq(comparator_17_eq));  // open: gt, lt
  Comparator #(.width(6), .mode("twosComplement")) comparator_18 (
    .a(in_4), .b(6'b100010), .eq(comparator_18_eq));  // open: gt, lt
  Comparator #(.width(6), .mode("twosComplement")) comparator_19 (
    .a(in_4), .b(6'b100000), .eq(comparator_19_eq));  // open: gt, lt
  Comparator #(.width(6), .mode("twosComplement")) comparator_20 (
    .a(in_4), .b(6'b101010), .eq(comparator_20_eq));  // open: gt, lt
  Comparator #(.width(6), .mode("twosComplement")) comparator_21 (
    .a(in_4), .b(6'b001100), .eq(comparator_21_eq));  // open: gt, lt
  Multiplexer #(.select(1), .width(4), .disabled("Z"), .enable("false")) multiplexer_1 (
    .in0(rom_1_data), .in1(\微程序地址转移逻辑_1_s0 ), .out(multiplexer_1_out), .sel(P));
  Register #(.width(4), .trigger("rising"), .Select("low")) register_1 (
    .D(multiplexer_1_out), .Q(Addr), .clk(CLK), .clr(RST));  // open: en
  and and_1 (JR, comparator_7_eq, comparator_6_eq);
  and and_2 (SRAV, comparator_8_eq, comparator_6_eq);
  and and_3 (SRLV, comparator_9_eq, comparator_6_eq);
  and and_4 (SLLV, comparator_10_eq, comparator_6_eq);
  and and_5 (SLL, comparator_11_eq, comparator_6_eq);
  and and_6 (SRL, comparator_12_eq, comparator_6_eq);
  and and_7 (SRA, comparator_13_eq, comparator_6_eq);
  and and_8 (NOR, comparator_14_eq, comparator_6_eq);
  and and_9 (XOR, comparator_15_eq, comparator_6_eq);
  and and_10 (OR, comparator_16_eq, comparator_6_eq);
  and and_11 (AND, comparator_17_eq, comparator_6_eq);
  and and_12 (SUB, comparator_18_eq, comparator_6_eq);
  and and_13 (ADD, comparator_19_eq, comparator_6_eq);
  and and_14 (SLT, comparator_20_eq, comparator_6_eq);
  and and_15 (SysCall, comparator_21_eq, comparator_6_eq);
  Multiplexer #(.select(1), .width(4), .disabled("Z"), .enable("false")) multiplexer_2 (
    .in0(4'b0101), .in1(4'b1011), .out(multiplexer_2_out), .sel(SLT));
  ROM #(.addrWidth(4), .dataWidth(21), .Select("high")) rom_1 (
    .addr(Addr),
    .data({IorD, PCsrc, AluSrcA, AluSrcB, MemToReg, RegDst, IrWrite, PcWrite, RegWrite, MemWrite, MemRead, Beq, Bne, ALU_Control, P, rom_1_data}));
  Multiplexer #(.select(1), .width(4), .disabled("Z"), .enable("false")) multiplexer_3 (
    .in0(multiplexer_2_out), .in1(4'b1010), .out(multiplexer_3_out), .sel(NOR));
  Multiplexer #(.select(1), .width(4), .disabled("Z"), .enable("false")) multiplexer_4 (
    .in0(multiplexer_3_out), .in1(4'b1001), .out(multiplexer_4_out), .sel(XOR));
  Multiplexer #(.select(1), .width(4), .disabled("Z"), .enable("false")) multiplexer_5 (
    .in0(multiplexer_4_out), .in1(4'b1000), .out(multiplexer_5_out), .sel(OR));
  Multiplexer #(.select(1), .width(4), .disabled("Z"), .enable("false")) multiplexer_6 (
    .in0(multiplexer_5_out), .in1(4'b0111), .out(multiplexer_6_out), .sel(AND));
  or or_1 (R_TYPE, SRAV, SRLV, SLLV, NOR, XOR, OR, AND, SUB, ADD, SLT);
  Multiplexer #(.select(1), .width(4), .disabled("Z"), .enable("false")) multiplexer_7 (
    .in0(multiplexer_6_out), .in1(4'b0110), .out(multiplexer_7_out), .sel(SUB));
  Multiplexer #(.select(1), .width(4), .disabled("Z"), .enable("false")) multiplexer_8 (
    .in0(multiplexer_7_out), .in1(4'b0101), .out(multiplexer_8_out), .sel(ADD));
  Multiplexer #(.select(1), .width(4), .disabled("Z"), .enable("false")) multiplexer_9 (
    .in0(multiplexer_8_out), .in1(4'b0010), .out(multiplexer_9_out), .sel(or_2_out));
  Multiplexer #(.select(1), .width(4), .disabled("Z"), .enable("false")) multiplexer_10 (
    .in0(multiplexer_9_out), .in1(4'b0001), .out(multiplexer_10_out), .sel(or_3_out));
  or or_2 (or_2_out, SRLV, SRL);
  or or_3 (or_3_out, SRA, SRAV);
  Multiplexer #(.select(1), .width(4), .disabled("Z"), .enable("false")) multiplexer_11 (
    .in0(multiplexer_10_out), .in1(4'b0000), .out(multiplexer_11_out), .sel(or_4_out));
  or or_4 (or_4_out, SLL, SLLV);
  Multiplexer #(.select(2), .width(4), .disabled("Z"), .enable("false")) multiplexer_12 (
    .in0(4'b0101), .in1(4'b0110), .in2(multiplexer_11_out), .in3(4'b0101), .out(ALU_OP), .sel(ALU_Control));

  // Other names for the same wires on the sheet: FUNC[5:0] = in_4

  // Notes on the sheet:
  //   指令译码信号
  //   根据指令进行微程序地址转移
  //   硬布线控制器内部架构
  //   直接地址
  //   微指令地址
  //   判断逻辑
  //   μAR
  //   算数右移
  //   rd=rt>>rs
  //   rd=rt<<rs
  //   或非rd=rs xor rd
  //   异或rd=!(rs|rt)
  //   微程序控制器
  //   contents of rom_1 (hex, n*v repeats v):
  //   13201 30010 60003 100204 8800 60006 100400 40048 4800 c0100 c0080 6000c 800 d
  //   微命令
  //   微指令
  //   ALU控制器逻辑
  //   直接地址
  //   判断逻辑
  //   指令译码逻辑
endmodule

// 地址转移逻辑
module \微程序地址转移逻辑  (
  input  R_Type,
  input  ADDI,
  input  LW,
  input  SW,
  input  BEQ,
  input  BNE,
  input  SYSCALL,
  output S3,
  output S2,
  output S1,
  output S0
);

  or or_1 (S3, ADDI, BEQ, BNE, SYSCALL);
  or or_2 (S2, R_Type, SW, SYSCALL);
  or or_3 (S1, R_Type, ADDI, LW, BNE);
  or or_4 (S0, R_Type, ADDI, SW, BEQ, SYSCALL);
endmodule

module MIPS_Regifile (
  input  [31:0] Din,
  input  Clk,
  input  WE,
  input  [4:0] R1_num,
  input  [4:0] W_num,
  input  [4:0] R2_num,
  output [31:0] R1,
  output [31:0] R2
);

  // RegisterFile registerfile_1: pin names not known; wires that end beside it: Din, Clk, WE, W_num, R1_num, R2_num, R1, R2

  // Notes on the sheet:
  //   寄存器堆的电路原理图
endmodule

// ALU
module MIPS_ALU (
  input  [31:0] X,
  input  [31:0] Y,
  input  [3:0] AluOP,
  output Equal,
  output [31:0] Result,
  output [31:0] Result_2
);

  wire [0:0] comparator_1_lt, comparator_2_lt;
  wire [31:0] adder_1_out, AND_out, divider_1_out, divider_1_rem, multiplier_1_cout, multiplier_1_out,
       NOR_out, OR_out, shifter_1_out, shifter_2_out, shifter_3_out, subtractor_1_out, XOR_out;

  Shifter #(.width(32), .shift("ll")) shifter_1 (.in(Y), .\dist (X[4:0]), .out(shifter_1_out));
  Shifter #(.width(32), .shift("ar")) shifter_2 (.in(Y), .\dist (X[4:0]), .out(shifter_2_out));
  Shifter #(.width(32), .shift("lr")) shifter_3 (.in(Y), .\dist (X[4:0]), .out(shifter_3_out));
  Multiplier #(.width(32)) multiplier_1 (.a(X), .b(Y), .out(multiplier_1_out), .cout(multiplier_1_cout));  // open: cin
  Divider #(.width(32)) divider_1 (.a(X), .b(Y), .out(divider_1_out), .rem(divider_1_rem));  // open: upper
  Adder #(.width(32)) adder_1 (.a(X), .b(Y), .out(adder_1_out));  // open: cin, cout
  Subtractor #(.width(32)) subtractor_1 (.a(X), .b(Y), .out(subtractor_1_out));  // open: bin, bout
  assign AND_out = X & Y;  // AND_Gate AND, 32 bits wide
  assign OR_out = X | Y;  // OR_Gate OR, 32 bits wide
  assign XOR_out = X ^ Y;  // XOR_Gate XOR, 32 bits wide
  assign NOR_out = ~(X | Y);  // NOR_Gate NOR, 32 bits wide
  Comparator #(.width(32), .mode("twosComplement")) comparator_1 (
    .a(X), .b(Y), .eq(Equal), .lt(comparator_1_lt[0]));  // open: gt
  Comparator #(.width(32), .mode("twosComplement")) comparator_2 (
    .a(X), .b(Y), .lt(comparator_2_lt[0]));  // open: gt, eq
  Multiplexer #(.select(4), .width(32), .disabled("Z"), .enable("false")) multiplexer_1 (
    .in0(shifter_1_out), .in1(shifter_2_out), .in2(shifter_3_out), .in3(multiplier_1_out),
    .in4(divider_1_out), .in5(adder_1_out), .in6(subtractor_1_out), .in7(AND_out), .in8(OR_out),
    .in9(XOR_out), .in10(NOR_out), .in11({{31{1'b0}}, comparator_1_lt[0]}),
    .in12({{31{1'b0}}, comparator_2_lt[0]}), .in13({32{1'b0}}), .in14({32{1'b0}}), .in15({32{1'b0}}),
    .out(Result), .sel(AluOP));
  Multiplexer #(.select(4), .width(32), .disabled("Z"), .enable("false")) multiplexer_2 (
    .in0({32{1'b0}}), .in1({32{1'b0}}), .in2({32{1'b0}}), .in3(multiplier_1_cout), .in4(divider_1_rem),
    .in5({32{1'b0}}), .in6({32{1'b0}}), .in7({32{1'b0}}), .in8({32{1'b0}}), .in9({32{1'b0}}),
    .in10({32{1'b0}}), .in11({32{1'b0}}), .in12({32{1'b0}}), .in13({32{1'b0}}), .in14({32{1'b0}}),
    .in15({32{1'b0}}), .out(Result_2), .sel(AluOP));

  // Other names for the same wires on the sheet: Result2[31:0] = Result_2; S[3:0] = AluOP

  // Notes on the sheet:
  //   不要改变此引脚区域内容，也不要改变ALU封装形式
  //   输入引脚
  //   输出引脚
  //   硬布线控制器内部逻辑
endmodule
