// Logisim project cpu-完成.circ as structural Verilog: 6 circuits, main circuit ◇单周期MIPS(硬布线)
module \单周期MIPS_硬布线  (
  output RegWrite,
  output MemWrite,
  output [31:0] PC,
  output [31:0] IR,
  output [31:0] RDin,
  output [31:0] MDin
);

  wire ALU_SRC, and_1_out, and_2_out, Beq, Bne, CLK, comparator_1_eq, halt, JAL, JMP, Jr, MemToReg,
       mips_alu_1_equal, not_1_out, RegDst, RST, SignedExt, SysCall, Tag;
  wire [3:0] ALU_OP;
  wire [4:0] multiplexer_4_out, multiplexer_5_out, multiplexer_6_out, multiplexer_8_out;
  wire [5:0] FUNC, OP;
  wire [15:0] \总周期数 ;
  wire [25:6] mips_probe_1_p2;
  wire [31:0] adder_1_out, adder_2_out, bit_extender_1_out, bit_extender_2_out, bit_extender_3_out,
       mips_alu_1_result, mips_regifile_1_r2, multiplexer_1_out, multiplexer_2_out, multiplexer_3_out,
       multiplexer_7_out, multiplexer_9_out, multiplexer_10_out, multiplexer_11_out, PC_q, R1, ram_1_data,
       shifter_1_out, shifter_2_out;

  Button \u_总复位  (.out(RST));
  Multiplexer #(.select(1), .width(32), .disabled("Z"), .enable("false")) multiplexer_1 (
    .in0(adder_1_out), .in1(adder_2_out), .out(multiplexer_1_out), .sel(Tag));
  Multiplexer #(.select(1), .width(32), .disabled("Z"), .enable("false")) multiplexer_2 (
    .in0(multiplexer_1_out), .in1(shifter_2_out), .out(multiplexer_2_out), .sel(JMP));
  Clock #(.highDuration(1), .lowDuration(1)) clock_1 (.out(CLK));
  \单周期硬布线控制器_part  \u_单周期硬布线控制器_1  (
    .Func(FUNC), .OP(OP), .ALU_OP(ALU_OP), .MemToReg(MemToReg), .MemWrite(MemWrite), .ALU_SRC(ALU_SRC),
    .RegWrite(RegWrite), .SysCALL(SysCall), .SignedExt(SignedExt), .RegDst(RegDst), .JR(Jr), .JMP(JMP),
    .Beq(Beq), .JAL(JAL), .Bne(Bne));
  Multiplexer #(.select(1), .width(32), .disabled("Z"), .enable("false")) multiplexer_3 (
    .in0(multiplexer_2_out), .in1(R1), .out(multiplexer_3_out), .sel(Jr));
  not not_1 (not_1_out, halt);
  Register #(.width(32), .trigger("rising"), .Select("low")) u_PC (
    .D(multiplexer_3_out), .en(not_1_out), .Q(PC_q), .clk(CLK), .clr(RST));
  // Probe on adder_2_out
  // Probe on \总周期数 
  // Probe on \总周期数 
  // Mips_Probe mips_probe_1: pin names not known; wires that end beside it: PC_q, {OP, mips_probe_1_p2, FUNC}
  Adder #(.width(32)) adder_1 (.a(PC_q), .b(32'h4), .out(adder_1_out));  // open: cin, cout
  // Probe on adder_1_out
  ROM #(.addrWidth(10), .dataWidth(32), .Select("low")) rom_1 (.addr(PC_q[11:2]), .data({OP, mips_probe_1_p2, FUNC}));
  // Probe on shifter_2_out
  // Probe on mips_probe_1_p2[25:21]
  // Probe on mips_probe_1_p2[20:16]
  // Probe on mips_probe_1_p2[15:11]
  assign bit_extender_1_out = {{16{1'b0}}, {mips_probe_1_p2[15:6], FUNC}};  // Bit_Extender bit_extender_1
  assign bit_extender_2_out = {{16{mips_probe_1_p2[15]}}, {mips_probe_1_p2[15:6], FUNC}};  // Bit_Extender bit_extender_2
  Multiplexer #(.select(1), .width(5), .disabled("Z"), .enable("false")) multiplexer_4 (
    .in0(mips_probe_1_p2[25:21]), .in1(5'b00010), .out(multiplexer_4_out), .sel(SysCall));
  Multiplexer #(.select(1), .width(5), .disabled("Z"), .enable("false")) multiplexer_5 (
    .in0(mips_probe_1_p2[20:16]), .in1(5'b00100), .out(multiplexer_5_out), .sel(SysCall));
  Multiplexer #(.select(1), .width(5), .disabled("Z"), .enable("false")) multiplexer_6 (
    .in0(mips_probe_1_p2[20:16]), .in1(mips_probe_1_p2[15:11]), .out(multiplexer_6_out), .sel(RegDst));
  Multiplexer #(.select(1), .width(32), .disabled("Z"), .enable("false")) multiplexer_7 (
    .in0(bit_extender_1_out), .in1(bit_extender_2_out), .out(multiplexer_7_out), .sel(SignedExt));
  assign bit_extender_3_out = {{6{1'b0}}, {mips_probe_1_p2, FUNC}};  // Bit_Extender bit_extender_3
  Multiplexer #(.select(1), .width(5), .disabled("Z"), .enable("false")) multiplexer_8 (
    .in0(multiplexer_6_out), .in1({5{1'b1}}), .out(multiplexer_8_out), .sel(JAL));
  Shifter #(.width(32), .shift("ll")) shifter_1 (.in(bit_extender_2_out), .\dist (5'b00010), .out(shifter_1_out));
  Adder #(.width(32)) adder_2 (.a(shifter_1_out), .b(adder_1_out), .out(adder_2_out));  // open: cin, cout
  Shifter #(.width(32), .shift("ll")) shifter_2 (.in(bit_extender_3_out), .\dist (5'b00010), .out(shifter_2_out));
  MIPS_Regifile mips_regifile_1 (
    .Din(multiplexer_11_out), .Clk(CLK), .R1(R1), .R2(mips_regifile_1_r2), .WE(RegWrite),
    .W_num(multiplexer_8_out), .R1_num(multiplexer_4_out), .R2_num(multiplexer_5_out));
  Multiplexer #(.select(1), .width(32), .disabled("Z"), .enable("false")) multiplexer_9 (
    .in0(mips_regifile_1_r2), .in1(multiplexer_7_out), .out(multiplexer_9_out), .sel(ALU_SRC));
  Comparator #(.width(32), .mode("twosComplement")) comparator_1 (
    .a(32'ha), .b(R1), .eq(comparator_1_eq));  // open: gt, lt
  and and_1 (and_1_out, mips_alu_1_equal, Beq);
  and and_2 (and_2_out, ~mips_alu_1_equal, Bne);  // AND_Gate
  MIPS_ALU mips_alu_1 (
    .X(R1), .Y(multiplexer_9_out), .AluOP(ALU_OP), .Equal(mips_alu_1_equal), .Result(mips_alu_1_result),
    .shamt(mips_probe_1_p2[10:6]));  // open: Result_2
  and and_3 (halt, SysCall, comparator_1_eq);
  or or_1 (Tag, and_1_out, and_2_out);
  RAM #(.addrWidth(10), .dataWidth(32), .bus("separate"), .Select("high")) ram_1 (
    .addr(mips_alu_1_result[11:2]), .din(mips_regifile_1_r2), .data(ram_1_data), .str(MemWrite), .clk(CLK),
    .clr(RST));  // open: sel, ld
  Multiplexer #(.select(1), .width(32), .disabled("Z"), .enable("false")) multiplexer_10 (
    .in0(mips_alu_1_result), .in1(ram_1_data), .out(multiplexer_10_out), .sel(MemToReg));
  Multiplexer #(.select(1), .width(32), .disabled("Z"), .enable("false")) multiplexer_11 (
    .in0(multiplexer_10_out), .in1(adder_1_out), .out(multiplexer_11_out), .sel(JAL));

  // Notes on the sheet:
  //   程序运行结束后可停机，查看数据存储器中80单元的排序情况是有符号降序
  //   总周期数参考值：224
  //   MIPS反汇编探针
  //   指令寄存器
  //   contents of rom_1 (hex, n*v repeats v):
  //   2010ffff 20110000 ae300000 22100001 22310004 ae300000 22100001 22310004 ae300000 22100001 22310004
  //   ae300000 22100001 22310004 ae300000 22100001 22310004 ae300000 22100001 22310004 ae300000 22100001
  //   22310004 ae300000 22100001 22310004 ae300000 22100001 22310004 ae300000 22100001 22310004 ae300000
  //   22100001 22310004 ae300000 22100001 22310004 ae300000 22100001 22310004 ae300000 22100001 22310004
  //   ae300000 22100001 22310004 ae300000 22100001 22310004 22100001 8020 2011003c 8e130000 8e340000
  //   274402a 11000002 ae330000 ae140000 2231fffc 1611fff8 102020 20020022 c 22100004 2011003c 1611fff2
  //   2002000a c
  //   Imm
  //   shamt
  //   为方便自动评测，需要输出PC，IR，寄存器文件写入端口RDin，内存写入端口MDin等信号，以上引脚不能悬空
  //   数据寄存器
endmodule

// 单周期硬布线控制器
module \单周期硬布线控制器  (
  input  [5:0] OP,
  input  [5:0] Func,
  output [3:0] ALU_OP,
  output MemToReg,
  output MemWrite,
  output ALU_SRC,
  output RegWrite,
  output SysCALL,
  output SignedExt,
  output RegDst,
  output Beq,
  output Bne,
  output JR,
  output JMP,
  output JAL
);

  wire ADD, ADDI, ADDIU, ADDU, AND, ANDI, comparator_12_eq, comparator_13_eq, comparator_14_eq,
       comparator_15_eq, comparator_16_eq, comparator_17_eq, comparator_18_eq, comparator_19_eq,
       comparator_20_eq, comparator_21_eq, comparator_22_eq, comparator_23_eq, comparator_24_eq,
       comparator_25_eq, comparator_26_eq, J, NOR, OR, or_2_out, or_4_out, or_5_out, or_8_out, or_9_out,
       or_11_out, ORI, SLL, SLT, SLTI, SLTU, SRA, SRL, SUB, \控制信号_1_alu_src , \控制信号_1_beq , \控制信号_1_bne ,
       \控制信号_1_jal , \控制信号_1_jr , \控制信号_1_jump , \控制信号_1_memtoreg , \控制信号_1_memwrite , \控制信号_1_regdst ,
       \控制信号_1_regwrite , \控制信号_1_signedext , \控制信号_1_syscall , \运算控制器_1_s0 , \运算控制器_1_s1 , \运算控制器_1_s2 ,
       \运算控制器_1_s3 ;
  wire [3:0] multiplexer_1_out;
  wire [5:0] undriven, undriven_2;

  Comparator #(.width(6), .mode("twosComplement")) comparator_1 (.a(OP), .b(6'b000010), .eq(J));  // open: gt, lt
  Comparator #(.width(6), .mode("twosComplement")) comparator_2 (.a(OP), .b(6'b000011), .eq(JAL));  // open: gt, lt
  Comparator #(.width(6), .mode("twosComplement")) comparator_3 (.a(OP), .b(6'b000100), .eq(Beq));  // open: gt, lt
  Comparator #(.width(6), .mode("twosComplement")) comparator_4 (.a(OP), .b(6'b000101), .eq(Bne));  // open: gt, lt
  Comparator #(.width(6), .mode("twosComplement")) comparator_5 (.a(OP), .b(6'b001000), .eq(ADDI));  // open: gt, lt
  Comparator #(.width(6), .mode("twosComplement")) comparator_6 (.a(OP), .b(6'b001100), .eq(ANDI));  // open: gt, lt
  Comparator #(.width(6), .mode("twosComplement")) comparator_7 (.a(OP), .b(6'b001001), .eq(ADDIU));  // open: gt, lt
  Comparator #(.width(6), .mode("twosComplement")) comparator_8 (.a(OP), .b(6'b001010), .eq(SLTI));  // open: gt, lt
  Comparator #(.width(6), .mode("twosComplement")) comparator_9 (.a(OP), .b(6'b001101), .eq(ORI));  // open: gt, lt
  Comparator #(.width(6), .mode("twosComplement")) comparator_10 (
    .a(OP), .b(6'b100011), .eq(MemToReg));  // open: gt, lt
  Comparator #(.width(6), .mode("twosComplement")) comparator_11 (
    .a(OP), .b(6'b101011), .eq(MemWrite));  // open: gt, lt
  Comparator #(.width(6), .mode("twosComplement")) comparator_12 (
    .a(OP), .b({6{1'b0}}), .eq(comparator_12_eq));  // open: gt, lt
  or or_1 (ALU_SRC, ADDI, ANDI, ADDIU, SLTI, ORI, MemToReg, MemWrite);
  or or_2 (or_2_out, ANDI, ADDIU, SLTI, ADDI, ORI, MemToReg, MemWrite);
  or or_3 (RegWrite, SLL, SRA, SRL, ADD, ADDU, SUB, AND, OR, NOR, SLT, SLTU, JAL, ADDI, ANDI, ADDIU, SLTI, ORI, MemToReg);
  Comparator #(.width(6), .mode("twosComplement")) comparator_13 (
    .a({Func[5:4], Func[4], Func[2:0]}), .b({6{1'b0}}), .eq(comparator_13_eq));  // open: gt, lt
  Comparator #(.width(6), .mode("twosComplement")) comparator_14 (
    .a({Func[5:4], Func[4], Func[2:0]}), .b(6'b000011), .eq(comparator_14_eq));  // open: gt, lt
  Comparator #(.width(6), .mode("twosComplement")) comparator_15 (
    .a({Func[5:4], Func[4], Func[2:0]}), .b(6'b000010), .eq(comparator_15_eq));  // open: gt, lt
  Comparator #(.width(6), .mode("twosComplement")) comparator_16 (
    .a({Func[5:4], Func[4], Func[2:0]}), .b(6'b100000), .eq(comparator_16_eq));  // open: gt, lt
  Comparator #(.width(6), .mode("twosComplement")) comparator_17 (
    .a({Func[5:4], Func[4], Func[2:0]}), .b(6'b100001), .eq(comparator_17_eq));  // open: gt, lt
  Comparator #(.width(6), .mode("twosComplement")) comparator_18 (
    .a({Func[5:4], Func[4], Func[2:0]}), .b(6'b100010), .eq(comparator_18_eq));  // open: gt, lt
  Comparator #(.width(6), .mode("twosComplement")) comparator_19 (
    .a({Func[5:4], Func[4], Func[2:0]}), .b(6'b100100), .eq(comparator_19_eq));  // open: gt, lt
  Comparator #(.width(6), .mode("twosComplement")) comparator_20 (
    .a({Func[5:4], Func[4], Func[2:0]}), .b(6'b100101), .eq(comparator_20_eq));  // open: gt, lt
  Comparator #(.width(6), .mode("twosComplement")) comparator_21 (
    .a({Func[5:4], Func[4], Func[2:0]}), .b(6'b100111), .eq(comparator_21_eq));  // open: gt, lt
  Comparator #(.width(6), .mode("twosComplement")) comparator_22 (
    .a({Func[5:4], Func[4], Func[2:0]}), .b(6'b101010), .eq(comparator_22_eq));  // open: gt, lt
  Comparator #(.width(6), .mode("twosComplement")) comparator_23 (
    .a({Func[5:4], Func[4], Func[2:0]}), .b(6'b101011), .eq(comparator_23_eq));  // open: gt, lt
  Comparator #(.width(6), .mode("twosComplement")) comparator_24 (
    .a({Func[5:4], Func[4], Func[2:0]}), .b(6'b001000), .eq(comparator_24_eq));  // open: gt, lt
  Comparator #(.width(6), .mode("twosComplement")) comparator_25 (
    .a({Func[5:4], Func[4], Func[2:0]}), .b(6'b001100), .eq(comparator_25_eq));  // open: gt, lt
  and and_1 (SLL, comparator_12_eq, comparator_13_eq);
  and and_2 (SRA, comparator_12_eq, comparator_14_eq);
  and and_3 (SRL, comparator_12_eq, comparator_15_eq);
  and and_4 (ADD, comparator_12_eq, comparator_16_eq);
  and and_5 (ADDU, comparator_12_eq, comparator_17_eq);
  and and_6 (SUB, comparator_12_eq, comparator_18_eq);
  and and_7 (AND, comparator_12_eq, comparator_19_eq);
  and and_8 (OR, comparator_12_eq, comparator_20_eq);
  and and_9 (NOR, comparator_12_eq, comparator_21_eq);
  and and_10 (SLT, comparator_12_eq, comparator_22_eq);
  and and_11 (SLTU, comparator_12_eq, comparator_23_eq);
  and and_12 (JR, comparator_12_eq, comparator_24_eq);
  and and_13 (SysCALL, comparator_12_eq, comparator_25_eq);
  or or_4 (or_4_out, SLL, SRA, SRL, ADD, ADDU, SUB, AND, OR, NOR, SLT, SLTU, JAL, ADDI, ANDI, ADDIU, SLTI, ORI, MemToReg);
  or or_5 (or_5_out, Beq, Bne, ADDI, ADDIU, SLTI);
  or or_6 (SignedExt, Beq, Bne, ADDI, ADDIU, SLTI);
  or or_7 (RegDst, SLL, SRA, SRL, ADD, ADDU, SUB, AND, OR, NOR, SLT, SLTU);
  or or_8 (or_8_out, SLL, SRA, SRL, ADD, ADDU, SUB, AND, OR, NOR, SLT, SLTU);
  or or_9 (or_9_out, JR, J, JAL);
  Comparator #(.width(6), .mode("twosComplement")) comparator_26 (
    .a({Func[5:4], Func[4], Func[2:0]}), .b(6'b101010), .eq(comparator_26_eq));  // open: gt, lt
  or or_10 (JMP, JR, J, JAL);
  \运算控制器  \u_运算控制器_1  (
    .OP0(OP[0]), .OP1(OP[1]), .OP2(OP[2]), .OP3(OP[3]), .OP4(OP[4]), .OP5(OP[5]), .F0(Func[0]), .F1(Func[1]),
    .F2(Func[2]), .F3(Func[4]), .F4(Func[4]), .F5(Func[5]), .S0(\运算控制器_1_s0 ), .S1(\运算控制器_1_s1 ),
    .S2(\运算控制器_1_s2 ), .S3(\运算控制器_1_s3 ));
  \控制信号  \u_控制信号_1  (
    .OP0(undriven[0]), .OP1(undriven[1]), .OP2(undriven[2]), .OP3(undriven[3]), .OP4(undriven[4]),
    .OP5(undriven[5]), .F0(undriven_2[0]), .F1(undriven_2[1]), .F2(undriven_2[2]), .F3(undriven_2[4]),
    .F4(undriven_2[4]), .F5(undriven_2[5]), .MemToReg(\控制信号_1_memtoreg ), .MemWrite(\控制信号_1_memwrite ),
    .ALU_SRC(\控制信号_1_alu_src ), .RegWrite(\控制信号_1_regwrite ), .SysCALL(\控制信号_1_syscall ),
    .SignedExt(\控制信号_1_signedext ), .RegDst(\控制信号_1_regdst ), .BEQ(\控制信号_1_beq ), .BNE(\控制信号_1_bne ),
    .JR(\控制信号_1_jr ), .JUMP(\控制信号_1_jump ), .JAL(\控制信号_1_jal ));
  Multiplexer #(.select(1), .width(4), .disabled("Z"), .enable("false")) multiplexer_1 (
    .in0(4'b0101), .in1(4'b1100), .out(multiplexer_1_out), .sel(comparator_26_eq));
  or or_11 (or_11_out, SRA, ADD, ADDU, AND, SLT, ADDI, ANDI, ADDIU, SLTI, MemToReg, MemWrite);
  or or_12 (ALU_OP[0], SRA, ADD, ADDU, AND, SLT, ADDI, ANDI, ADDIU, SLTI, MemToReg, MemWrite);
  // OR_Gate or_13 has open pins: in0=SRL, in1=SUB, in2=AND, in3=NOR, in4=SLT, in5=ANDI, in6=SLTI, out=open
  // OR_Gate or_14 has open pins: in0=ADD, in1=ADDU, in2=SUB, in3=AND, in4=SLTU, in5=ADDI, in6=ANDI, in7=ADDIU, in8=MemToReg, in9=MemWrite, out=open
  or or_15 (ALU_OP[1], SRL, SUB, AND, NOR, SLT, ANDI, SLTI);
  // OR_Gate or_16 has open pins: in0=OR, in1=NOR, in2=SLT, in3=SLTU, in4=SLTI, in5=ORI, out=open
  or or_17 (ALU_OP[2], ADD, ADDU, SUB, AND, SLTU, ADDI, ANDI, ADDIU, MemToReg, MemWrite);
  or or_18 (ALU_OP[3], OR, NOR, SLT, SLTU, SLTI, ORI);

  assign Func[3] = Func[4];

  // Other names for the same wires on the sheet: LW = MemToReg; SW = MemWrite

  // Notes on the sheet:
  //   指令译码信号
  //   指令译码逻辑
  //   注意R_TYPE表示R型运算指令，SYSCALL是特殊的R型指令，不属于这个类别
  //   给出简单的逻辑实现对应指令译码信号，LW、SW、BEQ、BNE、ADDI、ADD、SLT、SYSCALL、R_TYPE。
  //   根据指令译码信号实现控制器输出控制信号的逻辑
  //   ALU控制器逻辑
  //   给出简单的逻辑实现ALU_OP与OP、Func之间的对应关系
  //   控制信号
endmodule

module \运算控制器  (
  input  OP0,
  input  OP1,
  input  OP2,
  input  OP3,
  input  OP4,
  input  OP5,
  input  F0,
  input  F1,
  input  F2,
  input  F3,
  input  F4,
  input  F5,
  output S0,
  output S1,
  output S2,
  output S3
);

  wire and_1_out, and_2_out, and_3_out, and_4_out, and_5_out, and_6_out, and_7_out, and_8_out, and_9_out,
       and_10_out, and_11_out, and_12_out, and_13_out, and_14_out, and_15_out, and_16_out, and_17_out,
       and_18_out, and_19_out, and_20_out, and_21_out, and_22_out, and_23_out, and_24_out, and_25_out,
       and_26_out, and_27_out, and_28_out, and_29_out, and_30_out, and_31_out, and_32_out, and_33_out,
       and_34_out, not_1_out, not_2_out, not_3_out, not_4_out, not_5_out, not_6_out, not_7_out, not_8_out,
       not_9_out, not_10_out, not_11_out, not_12_out, not_13_out, not_14_out, not_15_out, not_16_out,
       not_17_out, not_18_out, not_19_out, not_20_out, not_21_out, not_22_out, not_23_out, not_24_out,
       not_25_out, not_26_out, not_27_out, not_28_out, not_29_out, not_30_out, not_31_out, not_32_out,
       not_33_out, not_34_out, not_35_out, not_36_out, not_37_out, not_38_out, not_39_out, not_40_out,
       not_41_out, not_42_out, not_43_out, not_44_out, not_45_out, not_46_out, not_47_out, not_48_out,
       not_49_out, not_50_out, not_51_out, not_52_out, not_53_out, not_54_out, not_55_out, not_56_out,
       not_57_out, not_58_out, not_59_out, not_60_out, not_61_out, not_62_out, not_63_out, not_64_out,
       not_65_out, not_66_out, not_67_out, not_68_out, not_69_out, not_70_out, not_71_out, not_72_out,
       not_73_out, not_74_out, not_75_out, not_76_out, not_77_out, not_78_out, not_79_out, not_80_out,
       not_81_out, not_82_out, not_83_out, not_84_out, not_85_out, not_86_out, not_87_out, not_88_out,
       not_89_out, not_90_out, not_91_out, not_92_out, not_93_out, not_94_out, not_95_out, not_96_out,
       not_97_out, not_98_out, not_99_out, not_100_out, not_101_out, not_102_out, not_103_out, not_104_out,
       not_105_out, not_106_out, not_107_out, not_108_out, not_109_out, not_110_out, not_111_out,
       not_112_out, not_113_out, not_114_out, not_115_out, not_116_out, not_117_out, not_118_out,
       not_119_out, not_120_out, not_121_out, not_122_out, not_123_out, not_124_out, not_125_out,
       not_126_out, not_127_out, not_128_out, not_129_out, not_130_out, not_131_out, not_132_out,
       not_133_out, not_134_out, not_135_out, not_136_out, not_137_out, not_138_out, not_139_out,
       not_140_out, not_141_out, not_142_out, not_143_out, not_144_out, not_145_out, not_146_out,
       not_147_out, not_148_out, not_149_out, not_150_out, not_151_out, not_152_out, not_153_out,
       not_154_out, not_155_out, not_156_out, not_157_out, not_158_out, not_159_out, not_160_out,
       not_161_out, not_162_out, not_163_out, not_164_out, not_165_out, not_166_out, not_167_out,
       not_168_out, not_169_out, not_170_out, not_171_out, not_172_out, not_173_out, not_174_out,
       not_175_out, not_176_out, not_177_out, not_178_out, not_179_out, not_180_out, not_181_out,
       not_182_out, not_183_out, not_184_out, not_185_out, not_186_out, not_187_out, not_188_out,
       not_189_out, not_190_out, not_191_out, not_192_out, not_193_out, not_194_out, not_195_out,
       not_196_out, not_197_out, not_198_out, not_199_out, not_200_out, not_201_out, not_202_out,
       not_203_out, not_204_out, not_205_out, not_206_out, not_207_out, not_208_out, not_209_out,
       not_210_out, not_211_out, not_212_out, not_213_out, not_214_out, not_215_out, not_216_out,
       not_217_out, not_218_out, not_219_out, not_220_out, not_221_out, not_222_out, not_223_out,
       not_224_out, not_225_out, not_226_out, not_227_out, not_228_out, not_229_out, not_230_out,
       not_231_out, not_232_out, not_233_out, not_234_out, not_235_out, not_236_out;

  not not_1 (not_1_out, OP5);
  not not_2 (not_2_out, OP4);
  not not_3 (not_3_out, OP3);
  not not_4 (not_4_out, OP2);
  not not_5 (not_5_out, OP1);
  not not_6 (not_6_out, OP0);
  not not_7 (not_7_out, F5);
  not not_8 (not_8_out, F4);
  not not_9 (not_9_out, F3);
  not not_10 (not_10_out, F2);
  not not_11 (not_11_out, OP5);
  not not_12 (not_12_out, OP4);
  not not_13 (not_13_out, OP3);
  not not_14 (not_14_out, OP2);
  not not_15 (not_15_out, OP1);
  not not_16 (not_16_out, OP0);
  not not_17 (not_17_out, F4);
  not not_18 (not_18_out, F3);
  not not_19 (not_19_out, F2);
  not not_20 (not_20_out, F1);
  not not_21 (not_21_out, F0);
  not not_22 (not_22_out, OP5);
  not not_23 (not_23_out, OP4);
  not not_24 (not_24_out, OP3);
  not not_25 (not_25_out, OP2);
  not not_26 (not_26_out, OP1);
  not not_27 (not_27_out, OP0);
  not not_28 (not_28_out, F4);
  not not_29 (not_29_out, F3);
  not not_30 (not_30_out, F2);
  not not_31 (not_31_out, F1);
  not not_32 (not_32_out, OP5);
  not not_33 (not_33_out, OP4);
  not not_34 (not_34_out, OP3);
  not not_35 (not_35_out, OP2);
  not not_36 (not_36_out, OP1);
  not not_37 (not_37_out, OP0);
  not not_38 (not_38_out, F4);
  not not_39 (not_39_out, F3);
  not not_40 (not_40_out, F1);
  not not_41 (not_41_out, F0);
  not not_42 (not_42_out, OP5);
  not not_43 (not_43_out, OP4);
  not not_44 (not_44_out, OP3);
  not not_45 (not_45_out, OP2);
  not not_46 (not_46_out, OP1);
  not not_47 (not_47_out, OP0);
  not not_48 (not_48_out, F4);
  not not_49 (not_49_out, F2);
  not not_50 (not_50_out, F0);
  not not_51 (not_51_out, OP5);
  not not_52 (not_52_out, OP4);
  not not_53 (not_53_out, OP2);
  not not_54 (not_54_out, OP1);
  not not_55 (not_55_out, OP0);
  not not_56 (not_56_out, OP5);
  not not_57 (not_57_out, OP4);
  not not_58 (not_58_out, OP1);
  not not_59 (not_59_out, OP0);
  not not_60 (not_60_out, OP5);
  not not_61 (not_61_out, OP4);
  not not_62 (not_62_out, OP2);
  not not_63 (not_63_out, OP1);
  not not_64 (not_64_out, OP5);
  not not_65 (not_65_out, OP4);
  not not_66 (not_66_out, OP2);
  not not_67 (not_67_out, OP0);
  not not_68 (not_68_out, OP4);
  not not_69 (not_69_out, OP3);
  not not_70 (not_70_out, OP2);
  not not_71 (not_71_out, OP4);
  not not_72 (not_72_out, OP2);
  not not_73 (not_73_out, OP5);
  not not_74 (not_74_out, OP4);
  not not_75 (not_75_out, OP3);
  not not_76 (not_76_out, OP2);
  not not_77 (not_77_out, OP1);
  not not_78 (not_78_out, OP0);
  not not_79 (not_79_out, F5);
  not not_80 (not_80_out, F4);
  not not_81 (not_81_out, F3);
  not not_82 (not_82_out, F2);
  not not_83 (not_83_out, F0);
  not not_84 (not_84_out, OP5);
  not not_85 (not_85_out, OP4);
  not not_86 (not_86_out, OP3);
  not not_87 (not_87_out, OP2);
  not not_88 (not_88_out, OP1);
  not not_89 (not_89_out, OP0);
  not not_90 (not_90_out, F4);
  not not_91 (not_91_out, F3);
  not not_92 (not_92_out, F2);
  not not_93 (not_93_out, F0);
  not not_94 (not_94_out, OP5);
  not not_95 (not_95_out, OP4);
  not not_96 (not_96_out, OP3);
  not not_97 (not_97_out, OP2);
  not not_98 (not_98_out, OP1);
  not not_99 (not_99_out, OP0);
  not not_100 (not_100_out, F4);
  not not_101 (not_101_out, F3);
  not not_102 (not_102_out, F1);
  not not_103 (not_103_out, F0);
  not not_104 (not_104_out, OP5);
  not not_105 (not_105_out, OP4);
  not not_106 (not_106_out, OP3);
  not not_107 (not_107_out, OP2);
  not not_108 (not_108_out, OP1);
  not not_109 (not_109_out, OP0);
  not not_110 (not_110_out, F4);
  not not_111 (not_111_out, F3);
  not not_112 (not_112_out, OP5);
  not not_113 (not_113_out, OP4);
  not not_114 (not_114_out, OP3);
  not not_115 (not_115_out, OP2);
  not not_116 (not_116_out, OP1);
  not not_117 (not_117_out, OP0);
  not not_118 (not_118_out, F4);
  not not_119 (not_119_out, F2);
  not not_120 (not_120_out, F0);
  not not_121 (not_121_out, OP5);
  not not_122 (not_122_out, OP4);
  not not_123 (not_123_out, OP1);
  not not_124 (not_124_out, OP0);
  not not_125 (not_125_out, OP5);
  not not_126 (not_126_out, OP4);
  not not_127 (not_127_out, OP2);
  not not_128 (not_128_out, OP0);
  not not_129 (not_129_out, OP5);
  not not_130 (not_130_out, OP4);
  not not_131 (not_131_out, OP3);
  not not_132 (not_132_out, OP2);
  not not_133 (not_133_out, OP1);
  not not_134 (not_134_out, OP0);
  not not_135 (not_135_out, F4);
  not not_136 (not_136_out, F3);
  not not_137 (not_137_out, F2);
  not not_138 (not_138_out, F1);
  not not_139 (not_139_out, F0);
  not not_140 (not_140_out, OP5);
  not not_141 (not_141_out, OP4);
  not not_142 (not_142_out, OP3);
  not not_143 (not_143_out, OP2);
  not not_144 (not_144_out, OP1);
  not not_145 (not_145_out, OP0);
  not not_146 (not_146_out, F4);
  not not_147 (not_147_out, F3);
  not not_148 (not_148_out, F2);
  not not_149 (not_149_out, F1);
  not not_150 (not_150_out, OP5);
  not not_151 (not_151_out, OP4);
  not not_152 (not_152_out, OP3);
  not not_153 (not_153_out, OP2);
  not not_154 (not_154_out, OP1);
  not not_155 (not_155_out, OP0);
  not not_156 (not_156_out, F4);
  not not_157 (not_157_out, F3);
  not not_158 (not_158_out, F2);
  not not_159 (not_159_out, F0);
  not not_160 (not_160_out, OP5);
  not not_161 (not_161_out, OP4);
  not not_162 (not_162_out, OP3);
  not not_163 (not_163_out, OP2);
  not not_164 (not_164_out, OP1);
  not not_165 (not_165_out, OP0);
  not not_166 (not_166_out, F4);
  not not_167 (not_167_out, F3);
  not not_168 (not_168_out, F1);
  not not_169 (not_169_out, F0);
  not not_170 (not_170_out, OP5);
  not not_171 (not_171_out, OP4);
  not not_172 (not_172_out, OP3);
  not not_173 (not_173_out, OP2);
  not not_174 (not_174_out, OP1);
  not not_175 (not_175_out, OP0);
  not not_176 (not_176_out, F4);
  not not_177 (not_177_out, F2);
  not not_178 (not_178_out, OP5);
  not not_179 (not_179_out, OP4);
  not not_180 (not_180_out, OP2);
  not not_181 (not_181_out, OP1);
  not not_182 (not_182_out, OP0);
  not not_183 (not_183_out, OP5);
  not not_184 (not_184_out, OP4);
  not not_185 (not_185_out, OP1);
  not not_186 (not_186_out, OP0);
  not not_187 (not_187_out, OP5);
  not not_188 (not_188_out, OP4);
  not not_189 (not_189_out, OP2);
  not not_190 (not_190_out, OP1);
  not not_191 (not_191_out, OP4);
  not not_192 (not_192_out, OP3);
  not not_193 (not_193_out, OP2);
  not not_194 (not_194_out, OP4);
  not not_195 (not_195_out, OP2);
  not not_196 (not_196_out, OP5);
  not not_197 (not_197_out, OP4);
  not not_198 (not_198_out, OP3);
  not not_199 (not_199_out, OP2);
  not not_200 (not_200_out, OP1);
  not not_201 (not_201_out, OP0);
  not not_202 (not_202_out, F4);
  not not_203 (not_203_out, F3);
  not not_204 (not_204_out, F1);
  not not_205 (not_205_out, OP5);
  not not_206 (not_206_out, OP4);
  not not_207 (not_207_out, OP3);
  not not_208 (not_208_out, OP2);
  not not_209 (not_209_out, OP1);
  not not_210 (not_210_out, OP0);
  not not_211 (not_211_out, F4);
  not not_212 (not_212_out, F3);
  not not_213 (not_213_out, OP5);
  not not_214 (not_214_out, OP4);
  not not_215 (not_215_out, OP3);
  not not_216 (not_216_out, OP2);
  not not_217 (not_217_out, OP1);
  not not_218 (not_218_out, OP0);
  not not_219 (not_219_out, F4);
  not not_220 (not_220_out, F2);
  not not_221 (not_221_out, F0);
  not not_222 (not_222_out, OP5);
  not not_223 (not_223_out, OP4);
  not not_224 (not_224_out, OP3);
  not not_225 (not_225_out, OP2);
  not not_226 (not_226_out, OP1);
  not not_227 (not_227_out, OP0);
  not not_228 (not_228_out, F4);
  not not_229 (not_229_out, F2);
  not not_230 (not_230_out, OP5);
  not not_231 (not_231_out, OP4);
  not not_232 (not_232_out, OP2);
  not not_233 (not_233_out, OP0);
  not not_234 (not_234_out, OP5);
  not not_235 (not_235_out, OP4);
  not not_236 (not_236_out, OP1);
  and and_1 (and_1_out, not_1_out, not_2_out, not_3_out, not_4_out, not_5_out, not_6_out, not_7_out, not_8_out, not_9_out, not_10_out, F1, F0);
  and and_2 (and_2_out, not_11_out, not_12_out, not_13_out, not_14_out, not_15_out, not_16_out, F5, not_17_out, not_18_out, not_19_out, not_20_out, not_21_out);
  and and_3 (and_3_out, not_22_out, not_23_out, not_24_out, not_25_out, not_26_out, not_27_out, F5, not_28_out, not_29_out, not_30_out, not_31_out, F0);
  and and_4 (and_4_out, not_32_out, not_33_out, not_34_out, not_35_out, not_36_out, not_37_out, F5, not_38_out, not_39_out, F2, not_40_out, not_41_out);
  and and_5 (and_5_out, not_42_out, not_43_out, not_44_out, not_45_out, not_46_out, not_47_out, F5, not_48_out, F3, not_49_out, F1, not_50_out);
  and and_6 (and_6_out, not_51_out, not_52_out, OP3, not_53_out, not_54_out, not_55_out);
  and and_7 (and_7_out, not_56_out, not_57_out, OP3, OP2, not_58_out, not_59_out);
  and and_8 (and_8_out, not_60_out, not_61_out, OP3, not_62_out, not_63_out, OP0);
  and and_9 (and_9_out, not_64_out, not_65_out, OP3, not_66_out, OP1, not_67_out);
  and and_10 (and_10_out, OP5, not_68_out, not_69_out, not_70_out, OP1, OP0);
  and and_11 (and_11_out, OP5, not_71_out, OP3, not_72_out, OP1, OP0);
  and and_12 (and_12_out, not_73_out, not_74_out, not_75_out, not_76_out, not_77_out, not_78_out, not_79_out, not_80_out, not_81_out, not_82_out, F1, not_83_out);
  and and_13 (and_13_out, not_84_out, not_85_out, not_86_out, not_87_out, not_88_out, not_89_out, F5, not_90_out, not_91_out, not_92_out, F1, not_93_out);
  and and_14 (and_14_out, not_94_out, not_95_out, not_96_out, not_97_out, not_98_out, not_99_out, F5, not_100_out, not_101_out, F2, not_102_out, not_103_out);
  and and_15 (and_15_out, not_104_out, not_105_out, not_106_out, not_107_out, not_108_out, not_109_out, F5, not_110_out, not_111_out, F2, F1, F0);
  and and_16 (and_16_out, not_112_out, not_113_out, not_114_out, not_115_out, not_116_out, not_117_out, F5, not_118_out, F3, not_119_out, F1, not_120_out);
  and and_17 (and_17_out, not_121_out, not_122_out, OP3, OP2, not_123_out, not_124_out);
  and and_18 (and_18_out, not_125_out, not_126_out, OP3, not_127_out, OP1, not_128_out);
  and and_19 (and_19_out, not_129_out, not_130_out, not_131_out, not_132_out, not_133_out, not_134_out, F5, not_135_out, not_136_out, not_137_out, not_138_out, not_139_out);
  and and_20 (and_20_out, not_140_out, not_141_out, not_142_out, not_143_out, not_144_out, not_145_out, F5, not_146_out, not_147_out, not_148_out, not_149_out, F0);
  and and_21 (and_21_out, not_150_out, not_151_out, not_152_out, not_153_out, not_154_out, not_155_out, F5, not_156_out, not_157_out, not_158_out, F1, not_159_out);
  and and_22 (and_22_out, not_160_out, not_161_out, not_162_out, not_163_out, not_164_out, not_165_out, F5, not_166_out, not_167_out, F2, not_168_out, not_169_out);
  and and_23 (and_23_out, not_170_out, not_171_out, not_172_out, not_173_out, not_174_out, not_175_out, F5, not_176_out, F3, not_177_out, F1, F0);
  and and_24 (and_24_out, not_178_out, not_179_out, OP3, not_180_out, not_181_out, not_182_out);
  and and_25 (and_25_out, not_183_out, not_184_out, OP3, OP2, not_185_out, not_186_out);
  and and_26 (and_26_out, not_187_out, not_188_out, OP3, not_189_out, not_190_out, OP0);
  and and_27 (and_27_out, OP5, not_191_out, not_192_out, not_193_out, OP1, OP0);
  and and_28 (and_28_out, OP5, not_194_out, OP3, not_195_out, OP1, OP0);
  and and_29 (and_29_out, not_196_out, not_197_out, not_198_out, not_199_out, not_200_out, not_201_out, F5, not_202_out, not_203_out, F2, not_204_out, F0);
  and and_30 (and_30_out, not_205_out, not_206_out, not_207_out, not_208_out, not_209_out, not_210_out, F5, not_211_out, not_212_out, F2, F1, F0);
  and and_31 (and_31_out, not_213_out, not_214_out, not_215_out, not_216_out, not_217_out, not_218_out, F5, not_219_out, F3, not_220_out, F1, not_221_out);
  and and_32 (and_32_out, not_222_out, not_223_out, not_224_out, not_225_out, not_226_out, not_227_out, F5, not_228_out, F3, not_229_out, F1, F0);
  and and_33 (and_33_out, not_230_out, not_231_out, OP3, not_232_out, OP1, not_233_out);
  and and_34 (and_34_out, not_234_out, not_235_out, OP3, OP2, not_236_out, OP0);
  or or_1 (S0, and_1_out, and_2_out, and_3_out, and_4_out, and_5_out, and_6_out, and_7_out, and_8_out, and_9_out, and_10_out, and_11_out);
  or or_2 (S1, and_12_out, and_13_out, and_14_out, and_15_out, and_16_out, and_17_out, and_18_out);
  or or_3 (S2, and_19_out, and_20_out, and_21_out, and_22_out, and_23_out, and_24_out, and_25_out, and_26_out, and_27_out, and_28_out);
  or or_4 (S3, and_29_out, and_30_out, and_31_out, and_32_out, and_33_out, and_34_out);
endmodule

// 控制信号生成
module \控制信号  (
  input  OP0,
  input  OP1,
  input  OP2,
  input  OP3,
  input  OP4,
  input  OP5,
  input  F0,
  input  F1,
  input  F2,
  input  F3,
  input  F4,
  input  F5,
  output MemToReg,
  output MemWrite,
  output ALU_SRC,
  output RegWrite,
  output SysCALL,
  output SignedExt,
  output RegDst,
  output BEQ,
  output BNE,
  output JR,
  output JUMP,
  output JAL
);

  wire and_3_out, and_4_out, and_5_out, and_6_out, and_7_out, and_8_out, and_9_out, and_10_out, and_11_out,
       and_12_out, and_13_out, and_14_out, and_15_out, and_16_out, and_17_out, and_18_out, and_19_out,
       and_20_out, and_21_out, and_22_out, and_23_out, and_24_out, and_25_out, and_26_out, and_27_out,
       and_29_out, and_30_out, and_31_out, and_32_out, and_33_out, and_34_out, and_35_out, and_36_out,
       and_37_out, and_38_out, and_39_out, and_40_out, and_41_out, and_42_out, and_43_out, and_44_out,
       and_48_out, and_49_out, and_50_out, not_1_out, not_2_out, not_3_out, not_4_out, not_5_out, not_6_out,
       not_7_out, not_8_out, not_9_out, not_10_out, not_11_out, not_12_out, not_13_out, not_14_out,
       not_15_out, not_16_out, not_17_out, not_18_out, not_19_out, not_20_out, not_21_out, not_22_out,
       not_23_out, not_24_out, not_25_out, not_26_out, not_27_out, not_28_out, not_29_out, not_30_out,
       not_31_out, not_32_out, not_33_out, not_34_out, not_35_out, not_36_out, not_37_out, not_38_out,
       not_39_out, not_40_out, not_41_out, not_42_out, not_43_out, not_44_out, not_45_out, not_46_out,
       not_47_out, not_48_out, not_49_out, not_50_out, not_51_out, not_52_out, not_53_out, not_54_out,
       not_55_out, not_56_out, not_57_out, not_58_out, not_59_out, not_60_out, not_61_out, not_62_out,
       not_63_out, not_64_out, not_65_out, not_66_out, not_67_out, not_68_out, not_69_out, not_70_out,
       not_71_out, not_72_out, not_73_out, not_74_out, not_75_out, not_76_out, not_77_out, not_78_out,
       not_79_out, not_80_out, not_81_out, not_82_out, not_83_out, not_84_out, not_85_out, not_86_out,
       not_87_out, not_88_out, not_89_out, not_90_out, not_91_out, not_92_out, not_93_out, not_94_out,
       not_95_out, not_96_out, not_97_out, not_98_out, not_99_out, not_100_out, not_101_out, not_102_out,
       not_103_out, not_104_out, not_105_out, not_106_out, not_107_out, not_108_out, not_109_out,
       not_110_out, not_111_out, not_112_out, not_113_out, not_114_out, not_115_out, not_116_out,
       not_117_out, not_118_out, not_119_out, not_120_out, not_121_out, not_122_out, not_123_out,
       not_124_out, not_125_out, not_126_out, not_127_out, not_128_out, not_129_out, not_130_out,
       not_131_out, not_132_out, not_133_out, not_134_out, not_135_out, not_136_out, not_137_out,
       not_138_out, not_139_out, not_140_out, not_141_out, not_142_out, not_143_out, not_144_out,
       not_145_out, not_146_out, not_147_out, not_148_out, not_149_out, not_150_out, not_151_out,
       not_152_out, not_153_out, not_154_out, not_155_out, not_156_out, not_157_out, not_158_out,
       not_159_out, not_160_out, not_161_out, not_162_out, not_163_out, not_164_out, not_165_out,
       not_166_out, not_167_out, not_168_out, not_169_out, not_170_out, not_171_out, not_172_out,
       not_173_out, not_174_out, not_175_out, not_176_out, not_177_out, not_178_out, not_179_out,
       not_180_out, not_181_out, not_182_out, not_183_out, not_184_out, not_185_out, not_186_out,
       not_187_out, not_188_out, not_189_out, not_190_out, not_191_out, not_192_out, not_193_out,
       not_194_out, not_195_out, not_196_out, not_197_out, not_198_out, not_199_out, not_200_out,
       not_201_out, not_202_out, not_203_out, not_204_out, not_205_out, not_206_out, not_207_out,
       not_208_out, not_209_out, not_210_out, not_211_out, not_212_out, not_213_out, not_214_out,
       not_215_out, not_216_out, not_217_out, not_218_out, not_219_out, not_220_out, not_221_out,
       not_222_out, not_223_out, not_224_out, not_225_out, not_226_out, not_227_out, not_228_out,
       not_229_out, not_230_out, not_231_out, not_232_out, not_233_out, not_234_out, not_235_out,
       not_236_out, not_237_out, not_238_out, not_239_out, not_240_out, not_241_out, not_242_out,
       not_243_out, not_244_out, not_245_out, not_246_out, not_247_out, not_248_out, not_249_out,
       not_250_out, not_251_out, not_252_out, not_253_out, not_254_out, not_255_out, not_256_out,
       not_257_out, not_258_out, not_259_out, not_260_out, not_261_out, not_262_out, not_263_out,
       not_264_out, not_265_out, not_266_out, not_267_out, not_268_out, not_269_out, not_270_out,
       not_271_out, not_272_out, not_273_out, not_274_out, not_275_out, not_276_out, not_277_out,
       not_278_out, not_279_out, not_280_out, not_281_out, not_282_out, not_283_out, not_284_out,
       not_285_out, not_286_out, not_287_out, not_288_out, not_289_out, not_290_out, not_291_out,
       not_292_out, not_293_out, not_294_out, not_295_out, not_296_out, not_297_out, not_298_out,
       not_299_out, not_300_out, not_301_out, not_302_out, not_303_out, not_304_out, not_305_out,
       not_306_out, not_307_out, not_308_out, not_309_out, not_310_out, not_311_out, not_312_out,
       not_313_out, not_314_out, not_315_out, not_316_out, not_317_out, not_318_out, not_319_out,
       not_320_out, not_321_out, not_322_out, not_323_out, not_324_out, not_325_out, not_326_out,
       not_327_out, not_328_out, not_329_out, not_330_out, not_331_out, not_332_out, not_333_out,
       not_334_out, not_335_out, not_336_out, not_337_out, not_338_out, not_339_out, not_340_out,
       not_341_out, not_342_out, not_343_out, not_344_out, not_345_out, not_346_out, not_347_out,
       not_348_out, not_349_out;

  not not_1 (not_1_out, OP4);
  not not_2 (not_2_out, OP3);
  not not_3 (not_3_out, OP2);
  not not_4 (not_4_out, OP4);
  not not_5 (not_5_out, OP2);
  not not_6 (not_6_out, OP5);
  not not_7 (not_7_out, OP4);
  not not_8 (not_8_out, OP2);
  not not_9 (not_9_out, OP1);
  not not_10 (not_10_out, OP0);
  not not_11 (not_11_out, OP5);
  not not_12 (not_12_out, OP4);
  not not_13 (not_13_out, OP1);
  not not_14 (not_14_out, OP0);
  not not_15 (not_15_out, OP5);
  not not_16 (not_16_out, OP4);
  not not_17 (not_17_out, OP2);
  not not_18 (not_18_out, OP1);
  not not_19 (not_19_out, OP5);
  not not_20 (not_20_out, OP4);
  not not_21 (not_21_out, OP2);
  not not_22 (not_22_out, OP0);
  not not_23 (not_23_out, OP5);
  not not_24 (not_24_out, OP4);
  not not_25 (not_25_out, OP1);
  not not_26 (not_26_out, OP4);
  not not_27 (not_27_out, OP3);
  not not_28 (not_28_out, OP2);
  not not_29 (not_29_out, OP4);
  not not_30 (not_30_out, OP2);
  not not_31 (not_31_out, OP5);
  not not_32 (not_32_out, OP4);
  not not_33 (not_33_out, OP3);
  not not_34 (not_34_out, OP2);
  not not_35 (not_35_out, OP1);
  not not_36 (not_36_out, OP0);
  not not_37 (not_37_out, F5);
  not not_38 (not_38_out, F4);
  not not_39 (not_39_out, F3);
  not not_40 (not_40_out, F2);
  not not_41 (not_41_out, F1);
  not not_42 (not_42_out, F0);
  not not_43 (not_43_out, OP5);
  not not_44 (not_44_out, OP4);
  not not_45 (not_45_out, OP3);
  not not_46 (not_46_out, OP2);
  not not_47 (not_47_out, OP1);
  not not_48 (not_48_out, OP0);
  not not_49 (not_49_out, F5);
  not not_50 (not_50_out, F4);
  not not_51 (not_51_out, F3);
  not not_52 (not_52_out, F2);
  not not_53 (not_53_out, OP5);
  not not_54 (not_54_out, OP4);
  not not_55 (not_55_out, OP3);
  not not_56 (not_56_out, OP2);
  not not_57 (not_57_out, OP1);
  not not_58 (not_58_out, OP0);
  not not_59 (not_59_out, F5);
  not not_60 (not_60_out, F4);
  not not_61 (not_61_out, F3);
  not not_62 (not_62_out, F2);
  not not_63 (not_63_out, F0);
  not not_64 (not_64_out, OP5);
  not not_65 (not_65_out, OP4);
  not not_66 (not_66_out, OP3);
  not not_67 (not_67_out, OP2);
  not not_68 (not_68_out, OP1);
  not not_69 (not_69_out, OP0);
  not not_70 (not_70_out, F4);
  not not_71 (not_71_out, F3);
  not not_72 (not_72_out, F2);
  not not_73 (not_73_out, F1);
  not not_74 (not_74_out, F0);
  not not_75 (not_75_out, OP5);
  not not_76 (not_76_out, OP4);
  not not_77 (not_77_out, OP3);
  not not_78 (not_78_out, OP2);
  not not_79 (not_79_out, OP1);
  not not_80 (not_80_out, OP0);
  not not_81 (not_81_out, F4);
  not not_82 (not_82_out, F3);
  not not_83 (not_83_out, F2);
  not not_84 (not_84_out, F1);
  not not_85 (not_85_out, OP5);
  not not_86 (not_86_out, OP4);
  not not_87 (not_87_out, OP3);
  not not_88 (not_88_out, OP2);
  not not_89 (not_89_out, OP1);
  not not_90 (not_90_out, OP0);
  not not_91 (not_91_out, F4);
  not not_92 (not_92_out, F3);
  not not_93 (not_93_out, F2);
  not not_94 (not_94_out, F0);
  not not_95 (not_95_out, OP5);
  not not_96 (not_96_out, OP4);
  not not_97 (not_97_out, OP3);
  not not_98 (not_98_out, OP2);
  not not_99 (not_99_out, OP1);
  not not_100 (not_100_out, OP0);
  not not_101 (not_101_out, F4);
  not not_102 (not_102_out, F3);
  not not_103 (not_103_out, F1);
  not not_104 (not_104_out, F0);
  not not_105 (not_105_out, OP5);
  not not_106 (not_106_out, OP4);
  not not_107 (not_107_out, OP3);
  not not_108 (not_108_out, OP2);
  not not_109 (not_109_out, OP1);
  not not_110 (not_110_out, OP0);
  not not_111 (not_111_out, F4);
  not not_112 (not_112_out, F3);
  not not_113 (not_113_out, F1);
  not not_114 (not_114_out, OP5);
  not not_115 (not_115_out, OP4);
  not not_116 (not_116_out, OP3);
  not not_117 (not_117_out, OP2);
  not not_118 (not_118_out, OP1);
  not not_119 (not_119_out, OP0);
  not not_120 (not_120_out, F4);
  not not_121 (not_121_out, F3);
  not not_122 (not_122_out, OP5);
  not not_123 (not_123_out, OP4);
  not not_124 (not_124_out, OP3);
  not not_125 (not_125_out, OP2);
  not not_126 (not_126_out, OP1);
  not not_127 (not_127_out, OP0);
  not not_128 (not_128_out, F4);
  not not_129 (not_129_out, F2);
  not not_130 (not_130_out, F0);
  not not_131 (not_131_out, OP5);
  not not_132 (not_132_out, OP4);
  not not_133 (not_133_out, OP3);
  not not_134 (not_134_out, OP2);
  not not_135 (not_135_out, OP1);
  not not_136 (not_136_out, OP0);
  not not_137 (not_137_out, F4);
  not not_138 (not_138_out, F2);
  not not_139 (not_139_out, OP5);
  not not_140 (not_140_out, OP4);
  not not_141 (not_141_out, OP3);
  not not_142 (not_142_out, OP2);
  not not_143 (not_143_out, OP5);
  not not_144 (not_144_out, OP4);
  not not_145 (not_145_out, OP2);
  not not_146 (not_146_out, OP1);
  not not_147 (not_147_out, OP0);
  not not_148 (not_148_out, OP5);
  not not_149 (not_149_out, OP4);
  not not_150 (not_150_out, OP1);
  not not_151 (not_151_out, OP0);
  not not_152 (not_152_out, OP5);
  not not_153 (not_153_out, OP4);
  not not_154 (not_154_out, OP2);
  not not_155 (not_155_out, OP1);
  not not_156 (not_156_out, OP5);
  not not_157 (not_157_out, OP4);
  not not_158 (not_158_out, OP2);
  not not_159 (not_159_out, OP0);
  not not_160 (not_160_out, OP5);
  not not_161 (not_161_out, OP4);
  not not_162 (not_162_out, OP1);
  not not_163 (not_163_out, OP4);
  not not_164 (not_164_out, OP3);
  not not_165 (not_165_out, OP2);
  not not_166 (not_166_out, OP5);
  not not_167 (not_167_out, OP4);
  not not_168 (not_168_out, OP3);
  not not_169 (not_169_out, OP2);
  not not_170 (not_170_out, OP1);
  not not_171 (not_171_out, OP0);
  not not_172 (not_172_out, F5);
  not not_173 (not_173_out, F4);
  not not_174 (not_174_out, F1);
  not not_175 (not_175_out, F0);
  not not_176 (not_176_out, OP5);
  not not_177 (not_177_out, OP4);
  not not_178 (not_178_out, OP3);
  not not_179 (not_179_out, OP1);
  not not_180 (not_180_out, OP0);
  not not_181 (not_181_out, OP5);
  not not_182 (not_182_out, OP4);
  not not_183 (not_183_out, OP3);
  not not_184 (not_184_out, OP1);
  not not_185 (not_185_out, OP5);
  not not_186 (not_186_out, OP4);
  not not_187 (not_187_out, OP2);
  not not_188 (not_188_out, OP1);
  not not_189 (not_189_out, OP0);
  not not_190 (not_190_out, OP5);
  not not_191 (not_191_out, OP4);
  not not_192 (not_192_out, OP2);
  not not_193 (not_193_out, OP1);
  not not_194 (not_194_out, OP5);
  not not_195 (not_195_out, OP4);
  not not_196 (not_196_out, OP2);
  not not_197 (not_197_out, OP0);
  not not_198 (not_198_out, OP5);
  not not_199 (not_199_out, OP4);
  not not_200 (not_200_out, OP3);
  not not_201 (not_201_out, OP2);
  not not_202 (not_202_out, OP1);
  not not_203 (not_203_out, OP0);
  not not_204 (not_204_out, F5);
  not not_205 (not_205_out, F4);
  not not_206 (not_206_out, F3);
  not not_207 (not_207_out, F2);
  not not_208 (not_208_out, F1);
  not not_209 (not_209_out, F0);
  not not_210 (not_210_out, OP5);
  not not_211 (not_211_out, OP4);
  not not_212 (not_212_out, OP3);
  not not_213 (not_213_out, OP2);
  not not_214 (not_214_out, OP1);
  not not_215 (not_215_out, OP0);
  not not_216 (not_216_out, F5);
  not not_217 (not_217_out, F4);
  not not_218 (not_218_out, F3);
  not not_219 (not_219_out, F2);
  not not_220 (not_220_out, OP5);
  not not_221 (not_221_out, OP4);
  not not_222 (not_222_out, OP3);
  not not_223 (not_223_out, OP2);
  not not_224 (not_224_out, OP1);
  not not_225 (not_225_out, OP0);
  not not_226 (not_226_out, F5);
  not not_227 (not_227_out, F4);
  not not_228 (not_228_out, F3);
  not not_229 (not_229_out, F2);
  not not_230 (not_230_out, F0);
  not not_231 (not_231_out, OP5);
  not not_232 (not_232_out, OP4);
  not not_233 (not_233_out, OP3);
  not not_234 (not_234_out, OP2);
  not not_235 (not_235_out, OP1);
  not not_236 (not_236_out, OP0);
  not not_237 (not_237_out, F4);
  not not_238 (not_238_out, F3);
  not not_239 (not_239_out, F2);
  not not_240 (not_240_out, F1);
  not not_241 (not_241_out, F0);
  not not_242 (not_242_out, OP5);
  not not_243 (not_243_out, OP4);
  not not_244 (not_244_out, OP3);
  not not_245 (not_245_out, OP2);
  not not_246 (not_246_out, OP1);
  not not_247 (not_247_out, OP0);
  not not_248 (not_248_out, F4);
  not not_249 (not_249_out, F3);
  not not_250 (not_250_out, F2);
  not not_251 (not_251_out, F1);
  not not_252 (not_252_out, OP5);
  not not_253 (not_253_out, OP4);
  not not_254 (not_254_out, OP3);
  not not_255 (not_255_out, OP2);
  not not_256 (not_256_out, OP1);
  not not_257 (not_257_out, OP0);
  not not_258 (not_258_out, F4);
  not not_259 (not_259_out, F3);
  not not_260 (not_260_out, F2);
  not not_261 (not_261_out, F0);
  not not_262 (not_262_out, OP5);
  not not_263 (not_263_out, OP4);
  not not_264 (not_264_out, OP3);
  not not_265 (not_265_out, OP2);
  not not_266 (not_266_out, OP1);
  not not_267 (not_267_out, OP0);
  not not_268 (not_268_out, F4);
  not not_269 (not_269_out, F3);
  not not_270 (not_270_out, F1);
  not not_271 (not_271_out, F0);
  not not_272 (not_272_out, OP5);
  not not_273 (not_273_out, OP4);
  not not_274 (not_274_out, OP3);
  not not_275 (not_275_out, OP2);
  not not_276 (not_276_out, OP1);
  not not_277 (not_277_out, OP0);
  not not_278 (not_278_out, F4);
  not not_279 (not_279_out, F3);
  not not_280 (not_280_out, F1);
  not not_281 (not_281_out, OP5);
  not not_282 (not_282_out, OP4);
  not not_283 (not_283_out, OP3);
  not not_284 (not_284_out, OP2);
  not not_285 (not_285_out, OP1);
  not not_286 (not_286_out, OP0);
  not not_287 (not_287_out, F4);
  not not_288 (not_288_out, F3);
  not not_289 (not_289_out, OP5);
  not not_290 (not_290_out, OP4);
  not not_291 (not_291_out, OP3);
  not not_292 (not_292_out, OP2);
  not not_293 (not_293_out, OP1);
  not not_294 (not_294_out, OP0);
  not not_295 (not_295_out, F4);
  not not_296 (not_296_out, F2);
  not not_297 (not_297_out, F0);
  not not_298 (not_298_out, OP5);
  not not_299 (not_299_out, OP4);
  not not_300 (not_300_out, OP3);
  not not_301 (not_301_out, OP2);
  not not_302 (not_302_out, OP1);
  not not_303 (not_303_out, OP0);
  not not_304 (not_304_out, F4);
  not not_305 (not_305_out, F2);
  not not_306 (not_306_out, OP5);
  not not_307 (not_307_out, OP4);
  not not_308 (not_308_out, OP3);
  not not_309 (not_309_out, OP1);
  not not_310 (not_310_out, OP0);
  not not_311 (not_311_out, OP5);
  not not_312 (not_312_out, OP4);
  not not_313 (not_313_out, OP3);
  not not_314 (not_314_out, OP1);
  not not_315 (not_315_out, OP5);
  not not_316 (not_316_out, OP4);
  not not_317 (not_317_out, OP3);
  not not_318 (not_318_out, OP2);
  not not_319 (not_319_out, OP1);
  not not_320 (not_320_out, OP0);
  not not_321 (not_321_out, F5);
  not not_322 (not_322_out, F4);
  not not_323 (not_323_out, F2);
  not not_324 (not_324_out, F1);
  not not_325 (not_325_out, F0);
  not not_326 (not_326_out, OP5);
  not not_327 (not_327_out, OP4);
  not not_328 (not_328_out, OP3);
  not not_329 (not_329_out, OP2);
  not not_330 (not_330_out, OP1);
  not not_331 (not_331_out, OP0);
  not not_332 (not_332_out, F5);
  not not_333 (not_333_out, F4);
  not not_334 (not_334_out, F2);
  not not_335 (not_335_out, F1);
  not not_336 (not_336_out, F0);
  not not_337 (not_337_out, OP5);
  not not_338 (not_338_out, OP4);
  not not_339 (not_339_out, OP3);
  not not_340 (not_340_out, OP2);
  not not_341 (not_341_out, OP0);
  not not_342 (not_342_out, OP5);
  not not_343 (not_343_out, OP4);
  not not_344 (not_344_out, OP3);
  not not_345 (not_345_out, OP2);
  not not_346 (not_346_out, OP5);
  not not_347 (not_347_out, OP4);
  not not_348 (not_348_out, OP3);
  not not_349 (not_349_out, OP2);
  and and_1 (MemToReg, OP5, not_1_out, not_2_out, not_3_out, OP1, OP0);
  and and_2 (MemWrite, OP5, not_4_out, OP3, not_5_out, OP1, OP0);
  and and_3 (and_3_out, not_6_out, not_7_out, OP3, not_8_out, not_9_out, not_10_out);
  and and_4 (and_4_out, not_11_out, not_12_out, OP3, OP2, not_13_out, not_14_out);
  and and_5 (and_5_out, not_15_out, not_16_out, OP3, not_17_out, not_18_out, OP0);
  and and_6 (and_6_out, not_19_out, not_20_out, OP3, not_21_out, OP1, not_22_out);
  and and_7 (and_7_out, not_23_out, not_24_out, OP3, OP2, not_25_out, OP0);
  and and_8 (and_8_out, OP5, not_26_out, not_27_out, not_28_out, OP1, OP0);
  and and_9 (and_9_out, OP5, not_29_out, OP3, not_30_out, OP1, OP0);
  and and_10 (and_10_out, not_31_out, not_32_out, not_33_out, not_34_out, not_35_out, not_36_out, not_37_out, not_38_out, not_39_out, not_40_out, not_41_out, not_42_out);
  and and_11 (and_11_out, not_43_out, not_44_out, not_45_out, not_46_out, not_47_out, not_48_out, not_49_out, not_50_out, not_51_out, not_52_out, F1, F0);
  and and_12 (and_12_out, not_53_out, not_54_out, not_55_out, not_56_out, not_57_out, not_58_out, not_59_out, not_60_out, not_61_out, not_62_out, F1, not_63_out);
  and and_13 (and_13_out, not_64_out, not_65_out, not_66_out, not_67_out, not_68_out, not_69_out, F5, not_70_out, not_71_out, not_72_out, not_73_out, not_74_out);
  and and_14 (and_14_out, not_75_out, not_76_out, not_77_out, not_78_out, not_79_out, not_80_out, F5, not_81_out, not_82_out, not_83_out, not_84_out, F0);
  and and_15 (and_15_out, not_85_out, not_86_out, not_87_out, not_88_out, not_89_out, not_90_out, F5, not_91_out, not_92_out, not_93_out, F1, not_94_out);
  and and_16 (and_16_out, not_95_out, not_96_out, not_97_out, not_98_out, not_99_out, not_100_out, F5, not_101_out, not_102_out, F2, not_103_out, not_104_out);
  and and_17 (and_17_out, not_105_out, not_106_out, not_107_out, not_108_out, not_109_out, not_110_out, F5, not_111_out, not_112_out, F2, not_113_out, F0);
  and and_18 (and_18_out, not_114_out, not_115_out, not_116_out, not_117_out, not_118_out, not_119_out, F5, not_120_out, not_121_out, F2, F1, F0);
  and and_19 (and_19_out, not_122_out, not_123_out, not_124_out, not_125_out, not_126_out, not_127_out, F5, not_128_out, F3, not_129_out, F1, not_130_out);
  and and_20 (and_20_out, not_131_out, not_132_out, not_133_out, not_134_out, not_135_out, not_136_out, F5, not_137_out, F3, not_138_out, F1, F0);
  and and_21 (and_21_out, not_139_out, not_140_out, not_141_out, not_142_out, OP1, OP0);
  and and_22 (and_22_out, not_143_out, not_144_out, OP3, not_145_out, not_146_out, not_147_out);
  and and_23 (and_23_out, not_148_out, not_149_out, OP3, OP2, not_150_out, not_151_out);
  and and_24 (and_24_out, not_152_out, not_153_out, OP3, not_154_out, not_155_out, OP0);
  and and_25 (and_25_out, not_156_out, not_157_out, OP3, not_158_out, OP1, not_159_out);
  and and_26 (and_26_out, not_160_out, not_161_out, OP3, OP2, not_162_out, OP0);
  and and_27 (and_27_out, OP5, not_163_out, not_164_out, not_165_out, OP1, OP0);
  and and_28 (SysCALL, not_166_out, not_167_out, not_168_out, not_169_out, not_170_out, not_171_out, not_172_out, not_173_out, F3, F2, not_174_out, not_175_out);
  and and_29 (and_29_out, not_176_out, not_177_out, not_178_out, OP2, not_179_out, not_180_out);
  and and_30 (and_30_out, not_181_out, not_182_out, not_183_out, OP2, not_184_out, OP0);
  and and_31 (and_31_out, not_185_out, not_186_out, OP3, not_187_out, not_188_out, not_189_out);
  and and_32 (and_32_out, not_190_out, not_191_out, OP3, not_192_out, not_193_out, OP0);
  and and_33 (and_33_out, not_194_out, not_195_out, OP3, not_196_out, OP1, not_197_out);
  and and_34 (and_34_out, not_198_out, not_199_out, not_200_out, not_201_out, not_202_out, not_203_out, not_204_out, not_205_out, not_206_out, not_207_out, not_208_out, not_209_out);
  and and_35 (and_35_out, not_210_out, not_211_out, not_212_out, not_213_out, not_214_out, not_215_out, not_216_out, not_217_out, not_218_out, not_219_out, F1, F0);
  and and_36 (and_36_out, not_220_out, not_221_out, not_222_out, not_223_out, not_224_out, not_225_out, not_226_out, not_227_out, not_228_out, not_229_out, F1, not_230_out);
  and and_37 (and_37_out, not_231_out, not_232_out, not_233_out, not_234_out, not_235_out, not_236_out, F5, not_237_out, not_238_out, not_239_out, not_240_out, not_241_out);
  and and_38 (and_38_out, not_242_out, not_243_out, not_244_out, not_245_out, not_246_out, not_247_out, F5, not_248_out, not_249_out, not_250_out, not_251_out, F0);
  and and_39 (and_39_out, not_252_out, not_253_out, not_254_out, not_255_out, not_256_out, not_257_out, F5, not_258_out, not_259_out, not_260_out, F1, not_261_out);
  and and_40 (and_40_out, not_262_out, not_263_out, not_264_out, not_265_out, not_266_out, not_267_out, F5, not_268_out, not_269_out, F2, not_270_out, not_271_out);
  and and_41 (and_41_out, not_272_out, not_273_out, not_274_out, not_275_out, not_276_out, not_277_out, F5, not_278_out, not_279_out, F2, not_280_out, F0);
  and and_42 (and_42_out, not_281_out, not_282_out, not_283_out, not_284_out, not_285_out, not_286_out, F5, not_287_out, not_288_out, F2, F1, F0);
  and and_43 (and_43_out, not_289_out, not_290_out, not_291_out, not_292_out, not_293_out, not_294_out, F5, not_295_out, F3, not_296_out, F1, not_297_out);
  and and_44 (and_44_out, not_298_out, not_299_out, not_300_out, not_301_out, not_302_out, not_303_out, F5, not_304_out, F3, not_305_out, F1, F0);
  and and_45 (BEQ, not_306_out, not_307_out, not_308_out, OP2, not_309_out, not_310_out);
  and and_46 (BNE, not_311_out, not_312_out, not_313_out, OP2, not_314_out, OP0);
  and and_47 (JR, not_315_out, not_316_out, not_317_out, not_318_out, not_319_out, not_320_out, not_321_out, not_322_out, F3, not_323_out, not_324_out, not_325_out);
  and and_48 (and_48_out, not_326_out, not_327_out, not_328_out, not_329_out, not_330_out, not_331_out, not_332_out, not_333_out, F3, not_334_out, not_335_out, not_336_out);
  and and_49 (and_49_out, not_337_out, not_338_out, not_339_out, not_340_out, OP1, not_341_out);
  and and_50 (and_50_out, not_342_out, not_343_out, not_344_out, not_345_out, OP1, OP0);
  and and_51 (JAL, not_346_out, not_347_out, not_348_out, not_349_out, OP1, OP0);
  or or_1 (ALU_SRC, and_3_out, and_4_out, and_5_out, and_6_out, and_7_out, and_8_out, and_9_out);
  or or_2 (SignedExt, and_29_out, and_30_out, and_31_out, and_32_out, and_33_out);
  or or_3 (RegDst, and_34_out, and_35_out, and_36_out, and_37_out, and_38_out, and_39_out, and_40_out, and_41_out, and_42_out, and_43_out, and_44_out);
  or or_4 (JUMP, and_48_out, and_49_out, and_50_out);
  or or_5 (RegWrite, and_10_out, and_11_out, and_12_out, and_13_out, and_14_out, and_15_out, and_16_out, and_17_out, and_18_out, and_19_out, and_20_out, and_21_out, and_22_out, and_23_out, and_24_out, and_25_out, and_26_out, and_27_out);
endmodule

module MIPS_Regifile (
  input  [31:0] Din,
  input  Clk,
  input  WE,
  input  [4:0] R1_num,
  input  [4:0] W_num,
  input  [4:0] R2_num,
  output [31:0] R1,
  output [31:0] R2
);

  // RegisterFile registerfile_1: pin names not known; wires that end beside it: Din, Clk, WE, W_num, R1_num, R2_num, R1, R2
endmodule

// ALU
module MIPS_ALU (
  input  [4:0] shamt,
  input  [31:0] X,
  input  [31:0] Y,
  input  [3:0] AluOP,
  output Equal,
  output [31:0] Result,
  output [31:0] Result_2
);

  wire [0:0] comparator_1_lt, comparator_2_lt;
  wire [31:0] adder_1_out, AND_out, divider_1_out, divider_1_rem, multiplier_1_cout, multiplier_1_out,
       NOR_out, OR_out, shifter_1_out, shifter_2_out, shifter_3_out, subtractor_1_out, XOR_out;

  assign AND_out = X & Y;  // AND_Gate AND, 32 bits wide
  assign OR_out = X | Y;  // OR_Gate OR, 32 bits wide
  Shifter #(.width(32), .shift("ll")) shifter_1 (.in(Y), .\dist (shamt), .out(shifter_1_out));
  Shifter #(.width(32), .shift("ar")) shifter_2 (.in(Y), .\dist (shamt), .out(shifter_2_out));
  Shifter #(.width(32), .shift("lr")) shifter_3 (.in(Y), .\dist (shamt), .out(shifter_3_out));
  Multiplier #(.width(32)) multiplier_1 (.a(X), .b(Y), .out(multiplier_1_out), .cout(multiplier_1_cout));  // open: cin
  Divider #(.width(32)) divider_1 (.a(X), .b(Y), .out(divider_1_out), .rem(divider_1_rem));  // open: upper
  Adder #(.width(32)) adder_1 (.a(X), .b(Y), .out(adder_1_out));  // open: cin, cout
  Subtractor #(.width(32)) subtractor_1 (.a(X), .b(Y), .out(subtractor_1_out));  // open: bin, bout
  assign XOR_out = X ^ Y;  // XOR_Gate XOR, 32 bits wide
  assign NOR_out = ~(X | Y);  // NOR_Gate NOR, 32 bits wide
  Comparator #(.width(32), .mode("twosComplement")) comparator_1 (
    .a(X), .b(Y), .eq(Equal), .lt(comparator_1_lt[0]));  // open: gt
  Comparator #(.width(32), .mode("unsigned")) comparator_2 (.a(X), .b(Y), .lt(comparator_2_lt[0]));  // open: gt, eq
  Multiplexer #(.select(4), .width(32), .disabled("Z"), .enable("false")) multiplexer_1 (
    .in0(shifter_1_out), .in1(shifter_2_out), .in2(shifter_3_out), .in3(multiplier_1_out),
    .in4(divider_1_out), .in5(adder_1_out), .in6(subtractor_1_out), .in7(AND_out), .in8(OR_out),
    .in9(XOR_out), .in10(NOR_out), .in11({{31{1'b0}}, comparator_1_lt[0]}),
    .in12({{31{1'b0}}, comparator_2_lt[0]}), .in13({32{1'b0}}), .in14({32{1'b0}}), .in15({32{1'b0}}),
    .out(Result), .sel(AluOP));
  Multiplexer #(.select(4), .width(32), .disabled("Z"), .enable("false")) multiplexer_2 (
    .in0({32{1'b0}}), .in1({32{1'b0}}), .in2({32{1'b0}}), .in3(multiplier_1_cout), .in4(divider_1_rem),
    .in5({32{1'b0}}), .in6({32{1'b0}}), .in7({32{1'b0}}), .in8({32{1'b0}}), .in9({32{1'b0}}),
    .in10({32{1'b0}}), .in11({32{1'b0}}), .in12({32{1'b0}}), .in13({32{1'b0}}), .in14({32{1'b0}}),
    .in15({32{1'b0}}), .out(Result_2), .sel(AluOP));

  // Other names for the same wires on the sheet: Result2[31:0] = Result_2; S[3:0] = AluOP

  // Notes on the sheet:
  //   不要改变此引脚区域内容，也不要改变ALU封装形式
  //   输入引脚
  //   输出引脚
endmodule
