// Logisim project 4 .单周期MIPS导教班实验-24条指令.circ as structural Verilog: 6 circuits, main circuit ◇单周期MIPS(硬布线)
module \单周期MIPS_硬布线  (
);

  wire and_1_out, and_2_out, Branch, CLK, comparator_1_eq, halt, JAL, JMP, Jr, LedOut, MemWrite,
       mips_alu_1_equal, not_1_out, not_2_out, or_2_out, RST, SignedExt, SysCall, \单周期硬布线控制器_1_alu_src ,
       \单周期硬布线控制器_1_beq , \单周期硬布线控制器_1_bne , \单周期硬布线控制器_1_memtoreg , \单周期硬布线控制器_1_regdst ,
       \单周期硬布线控制器_1_regwrite ;
  wire [3:0] \单周期硬布线控制器_1_alu_op ;
  wire [4:0] multiplexer_4_out, multiplexer_5_out, multiplexer_6_out, multiplexer_7_out;
  wire [15:0] \总周期数 , \无条件分支数 , \条件分支成功数 ;
  wire [27:2] rom_1_data;
  wire [31:0] adder_1_out, adder_2_out, bit_extender_1_out, bit_extender_2_out, LedData, mips_alu_1_result,
       mips_regifile_1_r1, mips_regifile_1_r2, multiplexer_1_out, multiplexer_2_out, multiplexer_3_out,
       multiplexer_8_out, multiplexer_9_out, multiplexer_10_out, multiplexer_11_out, PC_q, ram_1_data,
       shifter_1_out;
  wire [31:26] rom_1_data_2;

  Button \u_总复位  (.out(RST));
  Clock clock_1 (.out(CLK));
  Multiplexer #(.width(32), .enable("false")) multiplexer_1 (
    .in0(adder_1_out), .in1(adder_2_out), .out(multiplexer_1_out), .sel(Branch));
  Hex_Digit_Display hex_digit_display_1 (.value(LedData[27:24]));  // open: dp
  Hex_Digit_Display hex_digit_display_2 (.value(LedData[31:28]));  // open: dp
  Hex_Digit_Display hex_digit_display_3 (.value(LedData[31:28]));  // open: dp
  Multiplexer #(.width(32), .enable("false")) multiplexer_2 (
    .in0(multiplexer_1_out), .in1({4'b0000, rom_1_data, 2'b00}), .out(multiplexer_2_out), .sel(JMP));
  Multiplexer #(.width(32), .enable("false")) multiplexer_3 (
    .in0(multiplexer_2_out), .in1(mips_regifile_1_r1), .out(multiplexer_3_out), .sel(Jr));
  not not_1 (not_1_out, halt);
  Hex_Digit_Display hex_digit_display_4 (.value(LedData[23:20]));  // open: dp
  Hex_Digit_Display hex_digit_display_5 (.value(LedData[19:16]));  // open: dp
  Hex_Digit_Display hex_digit_display_6 (.value(LedData[27:24]));  // open: dp
  Hex_Digit_Display hex_digit_display_7 (.value(LedData[23:20]));  // open: dp
  Register #(.width(32)) PC (.D(multiplexer_3_out), .en(not_1_out), .Q(PC_q), .clk(CLK), .clr(RST));
  Hex_Digit_Display hex_digit_display_8 (.value(LedData[11:8]));  // open: dp
  Hex_Digit_Display hex_digit_display_9 (.value(LedData[15:12]));  // open: dp
  Hex_Digit_Display hex_digit_display_10 (.value(LedData[19:16]));  // open: dp
  Hex_Digit_Display hex_digit_display_11 (.value(LedData[15:12]));  // open: dp
  Hex_Digit_Display hex_digit_display_12 (.value(LedData[3:0]));  // open: dp
  Hex_Digit_Display hex_digit_display_13 (.value(LedData[7:4]));  // open: dp
  Hex_Digit_Display hex_digit_display_14 (.value(LedData[7:4]));  // open: dp
  Hex_Digit_Display hex_digit_display_15 (.value(LedData[11:8]));  // open: dp
  Adder #(.width(32)) adder_1 (.a(PC_q), .b(32'h4), .out(adder_1_out));  // open: cin, cout
  Hex_Digit_Display hex_digit_display_16 (.value(LedData[3:0]));  // open: dp
  ROM #(.addrWidth(10), .dataWidth(32)) rom_1 (.addr(PC_q[11:2]), .data({rom_1_data_2, rom_1_data}));  // open: sel
  // Probe on \总周期数 
  // Probe on \无条件分支数 
  // Probe on \条件分支成功数 
  \单周期硬布线控制器  \u_单周期硬布线控制器_1  (
    .Func(rom_1_data[7:2]), .OP(rom_1_data_2), .ALU_OP(\单周期硬布线控制器_1_alu_op ),
    .MemToReg(\单周期硬布线控制器_1_memtoreg ), .MemWrite(MemWrite), .ALU_SRC(\单周期硬布线控制器_1_alu_src ),
    .RegWrite(\单周期硬布线控制器_1_regwrite ), .SysCALL(SysCall), .SignedExt(SignedExt),
    .RegDst(\单周期硬布线控制器_1_regdst ), .JR(Jr), .JMP(JMP), .Beq(\单周期硬布线控制器_1_beq ), .JAL(JAL),
    .Bne(\单周期硬布线控制器_1_bne ));
  // Probe on multiplexer_4_out
  Multiplexer #(.width(5), .enable("false")) multiplexer_4 (
    .in0(rom_1_data[27:23]), .in1(5'b00010), .out(multiplexer_4_out), .sel(SysCall));
  // Probe on multiplexer_5_out
  Multiplexer #(.width(5), .enable("false")) multiplexer_5 (
    .in0(rom_1_data[22:18]), .in1(5'b00100), .out(multiplexer_5_out), .sel(SysCall));
  Multiplexer #(.width(5), .enable("false")) multiplexer_6 (
    .in0(rom_1_data[22:18]), .in1(rom_1_data[17:13]), .out(multiplexer_6_out), .sel(\单周期硬布线控制器_1_regdst ));
  Multiplexer #(.width(5), .enable("false")) multiplexer_7 (
    .in0(multiplexer_6_out), .in1({5{1'b1}}), .out(multiplexer_7_out), .sel(JAL));
  assign bit_extender_1_out = {{16{1'b0}}, rom_1_data[17:2]};  // Bit_Extender bit_extender_1
  assign bit_extender_2_out = {{16{rom_1_data[17]}}, rom_1_data[17:2]};  // Bit_Extender bit_extender_2
  // Probe on multiplexer_7_out
  Multiplexer #(.width(32), .enable("false")) multiplexer_8 (
    .in0(bit_extender_1_out), .in1(bit_extender_2_out), .out(multiplexer_8_out), .sel(SignedExt));
  Shifter #(.width(32)) shifter_1 (.in(bit_extender_2_out), .\dist (5'b00010), .out(shifter_1_out));
  Counter #(.width(16), .max('hffff)) counter_1 (
    .count(not_2_out), .Q(\总周期数 ), .clk(CLK), .clr(RST));  // open: load, D, carry
  not not_2 (not_2_out, halt);
  MIPS_Regifile mips_regifile_1 (
    .Din(multiplexer_11_out), .Clk(CLK), .R1(mips_regifile_1_r1), .R2(mips_regifile_1_r2),
    .WE(\单周期硬布线控制器_1_regwrite ), .W_num(multiplexer_7_out), .R1_num(multiplexer_4_out),
    .R2_num(multiplexer_5_out));
  Adder #(.width(32)) adder_2 (.a(shifter_1_out), .b(adder_1_out), .out(adder_2_out));  // open: cin, cout
  Multiplexer #(.width(32), .enable("false")) multiplexer_9 (
    .in0(mips_regifile_1_r2), .in1(multiplexer_8_out), .out(multiplexer_9_out), .sel(\单周期硬布线控制器_1_alu_src ));
  Counter #(.width(16), .max('hffff)) counter_2 (
    .count(Branch), .Q(\条件分支成功数 ), .clk(CLK), .clr(RST));  // open: load, D, carry
  MIPS_ALU mips_alu_1 (
    .X(mips_regifile_1_r1), .Y(multiplexer_9_out), .AluOP(\单周期硬布线控制器_1_alu_op ), .Equal(mips_alu_1_equal),
    .Result(mips_alu_1_result), .shamt(rom_1_data[12:8]));  // open: Result_2
  and and_1 (and_1_out, mips_alu_1_equal, \单周期硬布线控制器_1_beq );
  or or_1 (Branch, and_1_out, and_2_out);
  and and_2 (and_2_out, ~mips_alu_1_equal, \单周期硬布线控制器_1_bne );  // AND_Gate
  Comparator #(.width(32)) comparator_1 (.a(32'ha), .b(mips_regifile_1_r1), .eq(comparator_1_eq));  // open: gt, lt
  Register #(.width(32)) LedReg (.D(mips_regifile_1_r2), .en(LedOut), .Q(LedData), .clk(CLK));  // open: clr
  and and_3 (halt, SysCall, comparator_1_eq);
  and and_4 (LedOut, SysCall, ~comparator_1_eq);  // AND_Gate
  or or_2 (or_2_out, Jr, JMP);
  RAM #(.addrWidth(10), .dataWidth(32), .bus("separate")) ram_1 (
    .addr(mips_alu_1_result[11:2]), .din(mips_regifile_1_r2), .data(ram_1_data), .str(MemWrite), .clk(CLK),
    .clr(RST));  // open: sel, ld
  Counter #(.width(16), .max('hffff)) counter_3 (
    .count(or_2_out), .Q(\无条件分支数 ), .clk(CLK), .clr(RST));  // open: load, D, carry
  Multiplexer #(.width(32), .enable("false")) multiplexer_10 (
    .in0(mips_alu_1_result), .in1(ram_1_data), .out(multiplexer_10_out), .sel(\单周期硬布线控制器_1_memtoreg ));
  Multiplexer #(.width(32), .enable("false")) multiplexer_11 (
    .in0(multiplexer_10_out), .in1(adder_1_out), .out(multiplexer_11_out), .sel(JAL));

  // Notes on the sheet:
  //   Branch
  //   Jmp
  //   数码管输出应该用寄存器锁存，否则显示数据只能一闪而过
  //   Jr
  //   PC+Imm16<<2
  //   可以通过项目增加Logisim库的方式将前几次实验完成的电路作为子电路引入到本电路中使用
  //   数码管输出
  //   指令存储器
  //   PC+4
  //   伪直接寻址PC高4位+Imm26<<2
  //   OP
  //   rs
  //   rt
  //   指令字
  //   contents of rom_1 (hex, n*v repeats v):
  //   20110001 8000c05 20110001 20120002 20130003 8000c09 20110001 20120002 20130003 8000c0d 20110001
  //   20120002 20130003 8000c11 20110001 20120002 20130003 c000cb8 20100001 20110001 118fc0 112020
  //   20020022 c 118882 12200001 8000c15 112020 20020022 c 20110001 118880 112020 20020022 c 12200001
  //   8000c1f 20110001 118fc0 112020 20020022 c 1188c3 112020 20020022 c 118903 112020 20020022 c 118903
  //   112020 20020022 c 118903 112020 20020022 c 118903 112020 20020022 c 118903 112020 20020022 c 118903
  //   112020 20020022 c 118903 112020 20020022 c 20100001 109fc0 139fc3 8021 2012000c 24160003 26100001
  //   3210000f 20080008 20090001 139900 2709825 132020 20020022 c 1094022 1500fff9 22100001 2018000f
  //   2188024 108700 20080008 20090001 139902 2709825 132021 20020022 c 1094022 1500fff9 108702 2c9b022
  //   12c00001 8000c50 4020 1084027 84400 3508ffff 82021 20020022 c 2010ffff 20110000 ae300000 22100001
  //   22310004 ae300000 22100001 22310004 ae300000 22100001 22310004 ae300000 22100001 22310004 ae300000
  //   22100001 22310004 ae300000 22100001 22310004 ae300000 22100001 22310004 ae300000 22100001 22310004
  //   ae300000 22100001 22310004 ae300000 22100001 22310004 ae300000 22100001 22310004 ae300000 22100001
  //   22310004 ae300000 22100001 22310004 ae300000 22100001 22310004 ae300000 22100001 22310004 ae300000
  //   22100001 22310004 22100001 8020 2011003c 8e130000 8e340000 274402a 11000002 ae330000 ae140000
  //   2231fffc 1611fff8 102020 20020022 c 22100004 2011003c 1611fff2 2002000a c 20100000 22100001 102020
  //   20020022 c 22100002 102020 20020022 c 22100003 102020 20020022 c 22100004 102020 20020022 c 22100005
  //   102020 20020022 c 22100006 102020 20020022 c 22100007 102020 20020022 c 22100008 102020 20020022
  //   20020022 c 3e00008
  //   rd
  //   Imm16
  //   Imm26
  //   JMP
  //   JR
  //   Func
  //   shamt
  //   总复位信号应将除ROM以外所有存储组件全部清零
  //   Beq
  //   Bne
  //   MemToReg
  //   MemWrite
  //   AluOP
  //   AluSrcB
  //   RegWrite
  //   JAL
  //   RegDst
  //   IMM
  //   PC+Imm16<<2
  //   数据存储器
  //   MemToReg
  //   PC+4
endmodule

// 单周期硬布线控制器
module \单周期硬布线控制器  (
  input  [5:0] OP,
  input  [5:0] Func,
  output [3:0] ALU_OP,
  output MemToReg,
  output MemWrite,
  output ALU_SRC,
  output RegWrite,
  output SysCALL,
  output SignedExt,
  output RegDst,
  output Beq,
  output Bne,
  output JR,
  output JMP,
  output JAL
);

  \运算控制器自动生成  \u_运算控制器自动生成_1  (
    .OP0(OP[0]), .OP1(OP[1]), .OP2(OP[2]), .OP3(OP[3]), .OP4(OP[4]), .OP5(OP[5]), .F0(Func[0]), .F1(Func[1]),
    .F2(Func[2]), .F3(Func[3]), .F4(Func[4]), .F5(Func[5]), .S0(ALU_OP[0]), .S1(ALU_OP[1]), .S2(ALU_OP[2]),
    .S3(ALU_OP[3]));
  \控制信号自动生成  \u_控制信号自动生成_1  (
    .OP0(OP[0]), .OP1(OP[1]), .OP2(OP[2]), .OP3(OP[3]), .OP4(OP[4]), .OP5(OP[5]), .F0(Func[0]), .F1(Func[1]),
    .F2(Func[2]), .F3(Func[3]), .F4(Func[4]), .F5(Func[5]), .MemToReg(MemToReg), .MemWrite(MemWrite),
    .ALU_SRC(ALU_SRC), .RegWrite(RegWrite), .SysCALL(SysCALL), .SignedExt(SignedExt), .RegDst(RegDst),
    .BEQ(Beq), .BNE(Bne), .JR(JR), .JUMP(JMP), .JAL(JAL));

  // Other names for the same wires on the sheet: OP_CODE[5:0] = OP

  // Notes on the sheet:
  //   运算器控制器，根据指令生成运算器功能选择信号
  //   控制信号生成，产生数据通路需要的其他控制信号
endmodule

// 运算器控制器
module \运算控制器自动生成  (
  input  OP0,
  input  OP1,
  input  OP2,
  input  OP3,
  input  OP4,
  input  OP5,
  input  F0,
  input  F1,
  input  F2,
  input  F3,
  input  F4,
  input  F5,
  output S0,
  output S1,
  output S2,
  output S3
);

  wire and_1_out, and_2_out, and_3_out, and_4_out, and_5_out, and_6_out, and_7_out, and_8_out, and_9_out,
       and_10_out, and_11_out, and_12_out, and_13_out, and_14_out, and_15_out, and_16_out, and_17_out,
       and_18_out, and_19_out, and_20_out, and_21_out, and_22_out, and_23_out, and_24_out, and_25_out,
       and_26_out, and_27_out, and_28_out, and_29_out, and_30_out, and_31_out, and_32_out, and_33_out,
       and_34_out, not_1_out, not_2_out, not_3_out, not_4_out, not_5_out, not_6_out, not_7_out, not_8_out,
       not_9_out, not_10_out, not_11_out, not_12_out, not_13_out, not_14_out, not_15_out, not_16_out,
       not_17_out, not_18_out, not_19_out, not_20_out, not_21_out, not_22_out, not_23_out, not_24_out,
       not_25_out, not_26_out, not_27_out, not_28_out, not_29_out, not_30_out, not_31_out, not_32_out,
       not_33_out, not_34_out, not_35_out, not_36_out, not_37_out, not_38_out, not_39_out, not_40_out,
       not_41_out, not_42_out, not_43_out, not_44_out, not_45_out, not_46_out, not_47_out, not_48_out,
       not_49_out, not_50_out, not_51_out, not_52_out, not_53_out, not_54_out, not_55_out, not_56_out,
       not_57_out, not_58_out, not_59_out, not_60_out, not_61_out, not_62_out, not_63_out, not_64_out,
       not_65_out, not_66_out, not_67_out, not_68_out, not_69_out, not_70_out, not_71_out, not_72_out,
       not_73_out, not_74_out, not_75_out, not_76_out, not_77_out, not_78_out, not_79_out, not_80_out,
       not_81_out, not_82_out, not_83_out, not_84_out, not_85_out, not_86_out, not_87_out, not_88_out,
       not_89_out, not_90_out, not_91_out, not_92_out, not_93_out, not_94_out, not_95_out, not_96_out,
       not_97_out, not_98_out, not_99_out, not_100_out, not_101_out, not_102_out, not_103_out, not_104_out,
       not_105_out, not_106_out, not_107_out, not_108_out, not_109_out, not_110_out, not_111_out,
       not_112_out, not_113_out, not_114_out, not_115_out, not_116_out, not_117_out, not_118_out,
       not_119_out, not_120_out, not_121_out, not_122_out, not_123_out, not_124_out, not_125_out,
       not_126_out, not_127_out, not_128_out, not_129_out, not_130_out, not_131_out, not_132_out,
       not_133_out, not_134_out, not_135_out, not_136_out, not_137_out, not_138_out, not_139_out,
       not_140_out, not_141_out, not_142_out, not_143_out, not_144_out, not_145_out, not_146_out,
       not_147_out, not_148_out, not_149_out, not_150_out, not_151_out, not_152_out, not_153_out,
       not_154_out, not_155_out, not_156_out, not_157_out, not_158_out, not_159_out, not_160_out,
       not_161_out, not_162_out, not_163_out, not_164_out, not_165_out, not_166_out, not_167_out,
       not_168_out, not_169_out, not_170_out, not_171_out, not_172_out, not_173_out, not_174_out,
       not_175_out, not_176_out, not_177_out, not_178_out, not_179_out, not_180_out, not_181_out,
       not_182_out, not_183_out, not_184_out, not_185_out, not_186_out, not_187_out, not_188_out,
       not_189_out, not_190_out, not_191_out, not_192_out, not_193_out, not_194_out, not_195_out,
       not_196_out, not_197_out, not_198_out, not_199_out, not_200_out, not_201_out, not_202_out,
       not_203_out, not_204_out, not_205_out, not_206_out, not_207_out, not_208_out, not_209_out,
       not_210_out, not_211_out, not_212_out, not_213_out, not_214_out, not_215_out, not_216_out,
       not_217_out, not_218_out, not_219_out, not_220_out, not_221_out, not_222_out, not_223_out,
       not_224_out, not_225_out, not_226_out, not_227_out, not_228_out, not_229_out, not_230_out,
       not_231_out, not_232_out, not_233_out, not_234_out, not_235_out, not_236_out;

  not not_1 (not_1_out, OP5);
  not not_2 (not_2_out, OP4);
  not not_3 (not_3_out, OP3);
  not not_4 (not_4_out, OP2);
  not not_5 (not_5_out, OP1);
  not not_6 (not_6_out, OP0);
  not not_7 (not_7_out, F5);
  not not_8 (not_8_out, F4);
  not not_9 (not_9_out, F3);
  not not_10 (not_10_out, F2);
  not not_11 (not_11_out, OP5);
  not not_12 (not_12_out, OP4);
  not not_13 (not_13_out, OP3);
  not not_14 (not_14_out, OP2);
  not not_15 (not_15_out, OP1);
  not not_16 (not_16_out, OP0);
  not not_17 (not_17_out, F4);
  not not_18 (not_18_out, F3);
  not not_19 (not_19_out, F2);
  not not_20 (not_20_out, F1);
  not not_21 (not_21_out, F0);
  not not_22 (not_22_out, OP5);
  not not_23 (not_23_out, OP4);
  not not_24 (not_24_out, OP3);
  not not_25 (not_25_out, OP2);
  not not_26 (not_26_out, OP1);
  not not_27 (not_27_out, OP0);
  not not_28 (not_28_out, F4);
  not not_29 (not_29_out, F3);
  not not_30 (not_30_out, F2);
  not not_31 (not_31_out, F1);
  not not_32 (not_32_out, OP5);
  not not_33 (not_33_out, OP4);
  not not_34 (not_34_out, OP3);
  not not_35 (not_35_out, OP2);
  not not_36 (not_36_out, OP1);
  not not_37 (not_37_out, OP0);
  not not_38 (not_38_out, F4);
  not not_39 (not_39_out, F3);
  not not_40 (not_40_out, F1);
  not not_41 (not_41_out, F0);
  not not_42 (not_42_out, OP5);
  not not_43 (not_43_out, OP4);
  not not_44 (not_44_out, OP3);
  not not_45 (not_45_out, OP2);
  not not_46 (not_46_out, OP1);
  not not_47 (not_47_out, OP0);
  not not_48 (not_48_out, F4);
  not not_49 (not_49_out, F2);
  not not_50 (not_50_out, F0);
  not not_51 (not_51_out, OP5);
  not not_52 (not_52_out, OP4);
  not not_53 (not_53_out, OP2);
  not not_54 (not_54_out, OP1);
  not not_55 (not_55_out, OP0);
  not not_56 (not_56_out, OP5);
  not not_57 (not_57_out, OP4);
  not not_58 (not_58_out, OP1);
  not not_59 (not_59_out, OP0);
  not not_60 (not_60_out, OP5);
  not not_61 (not_61_out, OP4);
  not not_62 (not_62_out, OP2);
  not not_63 (not_63_out, OP1);
  not not_64 (not_64_out, OP5);
  not not_65 (not_65_out, OP4);
  not not_66 (not_66_out, OP2);
  not not_67 (not_67_out, OP0);
  not not_68 (not_68_out, OP4);
  not not_69 (not_69_out, OP3);
  not not_70 (not_70_out, OP2);
  not not_71 (not_71_out, OP4);
  not not_72 (not_72_out, OP2);
  not not_73 (not_73_out, OP5);
  not not_74 (not_74_out, OP4);
  not not_75 (not_75_out, OP3);
  not not_76 (not_76_out, OP2);
  not not_77 (not_77_out, OP1);
  not not_78 (not_78_out, OP0);
  not not_79 (not_79_out, F5);
  not not_80 (not_80_out, F4);
  not not_81 (not_81_out, F3);
  not not_82 (not_82_out, F2);
  not not_83 (not_83_out, F0);
  not not_84 (not_84_out, OP5);
  not not_85 (not_85_out, OP4);
  not not_86 (not_86_out, OP3);
  not not_87 (not_87_out, OP2);
  not not_88 (not_88_out, OP1);
  not not_89 (not_89_out, OP0);
  not not_90 (not_90_out, F4);
  not not_91 (not_91_out, F3);
  not not_92 (not_92_out, F2);
  not not_93 (not_93_out, F0);
  not not_94 (not_94_out, OP5);
  not not_95 (not_95_out, OP4);
  not not_96 (not_96_out, OP3);
  not not_97 (not_97_out, OP2);
  not not_98 (not_98_out, OP1);
  not not_99 (not_99_out, OP0);
  not not_100 (not_100_out, F4);
  not not_101 (not_101_out, F3);
  not not_102 (not_102_out, F1);
  not not_103 (not_103_out, F0);
  not not_104 (not_104_out, OP5);
  not not_105 (not_105_out, OP4);
  not not_106 (not_106_out, OP3);
  not not_107 (not_107_out, OP2);
  not not_108 (not_108_out, OP1);
  not not_109 (not_109_out, OP0);
  not not_110 (not_110_out, F4);
  not not_111 (not_111_out, F3);
  not not_112 (not_112_out, OP5);
  not not_113 (not_113_out, OP4);
  not not_114 (not_114_out, OP3);
  not not_115 (not_115_out, OP2);
  not not_116 (not_116_out, OP1);
  not not_117 (not_117_out, OP0);
  not not_118 (not_118_out, F4);
  not not_119 (not_119_out, F2);
  not not_120 (not_120_out, F0);
  not not_121 (not_121_out, OP5);
  not not_122 (not_122_out, OP4);
  not not_123 (not_123_out, OP1);
  not not_124 (not_124_out, OP0);
  not not_125 (not_125_out, OP5);
  not not_126 (not_126_out, OP4);
  not not_127 (not_127_out, OP2);
  not not_128 (not_128_out, OP0);
  not not_129 (not_129_out, OP5);
  not not_130 (not_130_out, OP4);
  not not_131 (not_131_out, OP3);
  not not_132 (not_132_out, OP2);
  not not_133 (not_133_out, OP1);
  not not_134 (not_134_out, OP0);
  not not_135 (not_135_out, F4);
  not not_136 (not_136_out, F3);
  not not_137 (not_137_out, F2);
  not not_138 (not_138_out, F1);
  not not_139 (not_139_out, F0);
  not not_140 (not_140_out, OP5);
  not not_141 (not_141_out, OP4);
  not not_142 (not_142_out, OP3);
  not not_143 (not_143_out, OP2);
  not not_144 (not_144_out, OP1);
  not not_145 (not_145_out, OP0);
  not not_146 (not_146_out, F4);
  not not_147 (not_147_out, F3);
  not not_148 (not_148_out, F2);
  not not_149 (not_149_out, F1);
  not not_150 (not_150_out, OP5);
  not not_151 (not_151_out, OP4);
  not not_152 (not_152_out, OP3);
  not not_153 (not_153_out, OP2);
  not not_154 (not_154_out, OP1);
  not not_155 (not_155_out, OP0);
  not not_156 (not_156_out, F4);
  not not_157 (not_157_out, F3);
  not not_158 (not_158_out, F2);
  not not_159 (not_159_out, F0);
  not not_160 (not_160_out, OP5);
  not not_161 (not_161_out, OP4);
  not not_162 (not_162_out, OP3);
  not not_163 (not_163_out, OP2);
  not not_164 (not_164_out, OP1);
  not not_165 (not_165_out, OP0);
  not not_166 (not_166_out, F4);
  not not_167 (not_167_out, F3);
  not not_168 (not_168_out, F1);
  not not_169 (not_169_out, F0);
  not not_170 (not_170_out, OP5);
  not not_171 (not_171_out, OP4);
  not not_172 (not_172_out, OP3);
  not not_173 (not_173_out, OP2);
  not not_174 (not_174_out, OP1);
  not not_175 (not_175_out, OP0);
  not not_176 (not_176_out, F4);
  not not_177 (not_177_out, F2);
  not not_178 (not_178_out, OP5);
  not not_179 (not_179_out, OP4);
  not not_180 (not_180_out, OP2);
  not not_181 (not_181_out, OP1);
  not not_182 (not_182_out, OP0);
  not not_183 (not_183_out, OP5);
  not not_184 (not_184_out, OP4);
  not not_185 (not_185_out, OP1);
  not not_186 (not_186_out, OP0);
  not not_187 (not_187_out, OP5);
  not not_188 (not_188_out, OP4);
  not not_189 (not_189_out, OP2);
  not not_190 (not_190_out, OP1);
  not not_191 (not_191_out, OP4);
  not not_192 (not_192_out, OP3);
  not not_193 (not_193_out, OP2);
  not not_194 (not_194_out, OP4);
  not not_195 (not_195_out, OP2);
  not not_196 (not_196_out, OP5);
  not not_197 (not_197_out, OP4);
  not not_198 (not_198_out, OP3);
  not not_199 (not_199_out, OP2);
  not not_200 (not_200_out, OP1);
  not not_201 (not_201_out, OP0);
  not not_202 (not_202_out, F4);
  not not_203 (not_203_out, F3);
  not not_204 (not_204_out, F1);
  not not_205 (not_205_out, OP5);
  not not_206 (not_206_out, OP4);
  not not_207 (not_207_out, OP3);
  not not_208 (not_208_out, OP2);
  not not_209 (not_209_out, OP1);
  not not_210 (not_210_out, OP0);
  not not_211 (not_211_out, F4);
  not not_212 (not_212_out, F3);
  not not_213 (not_213_out, OP5);
  not not_214 (not_214_out, OP4);
  not not_215 (not_215_out, OP3);
  not not_216 (not_216_out, OP2);
  not not_217 (not_217_out, OP1);
  not not_218 (not_218_out, OP0);
  not not_219 (not_219_out, F4);
  not not_220 (not_220_out, F2);
  not not_221 (not_221_out, F0);
  not not_222 (not_222_out, OP5);
  not not_223 (not_223_out, OP4);
  not not_224 (not_224_out, OP3);
  not not_225 (not_225_out, OP2);
  not not_226 (not_226_out, OP1);
  not not_227 (not_227_out, OP0);
  not not_228 (not_228_out, F4);
  not not_229 (not_229_out, F2);
  not not_230 (not_230_out, OP5);
  not not_231 (not_231_out, OP4);
  not not_232 (not_232_out, OP2);
  not not_233 (not_233_out, OP0);
  not not_234 (not_234_out, OP5);
  not not_235 (not_235_out, OP4);
  not not_236 (not_236_out, OP1);
  and and_1 (and_1_out, not_1_out, not_2_out, not_3_out, not_4_out, not_5_out, not_6_out, not_7_out, not_8_out, not_9_out, not_10_out, F1, F0);
  and and_2 (and_2_out, not_11_out, not_12_out, not_13_out, not_14_out, not_15_out, not_16_out, F5, not_17_out, not_18_out, not_19_out, not_20_out, not_21_out);
  and and_3 (and_3_out, not_22_out, not_23_out, not_24_out, not_25_out, not_26_out, not_27_out, F5, not_28_out, not_29_out, not_30_out, not_31_out, F0);
  and and_4 (and_4_out, not_32_out, not_33_out, not_34_out, not_35_out, not_36_out, not_37_out, F5, not_38_out, not_39_out, F2, not_40_out, not_41_out);
  and and_5 (and_5_out, not_42_out, not_43_out, not_44_out, not_45_out, not_46_out, not_47_out, F5, not_48_out, F3, not_49_out, F1, not_50_out);
  and and_6 (and_6_out, not_51_out, not_52_out, OP3, not_53_out, not_54_out, not_55_out);
  and and_7 (and_7_out, not_56_out, not_57_out, OP3, OP2, not_58_out, not_59_out);
  and and_8 (and_8_out, not_60_out, not_61_out, OP3, not_62_out, not_63_out, OP0);
  and and_9 (and_9_out, not_64_out, not_65_out, OP3, not_66_out, OP1, not_67_out);
  and and_10 (and_10_out, OP5, not_68_out, not_69_out, not_70_out, OP1, OP0);
  and and_11 (and_11_out, OP5, not_71_out, OP3, not_72_out, OP1, OP0);
  and and_12 (and_12_out, not_73_out, not_74_out, not_75_out, not_76_out, not_77_out, not_78_out, not_79_out, not_80_out, not_81_out, not_82_out, F1, not_83_out);
  and and_13 (and_13_out, not_84_out, not_85_out, not_86_out, not_87_out, not_88_out, not_89_out, F5, not_90_out, not_91_out, not_92_out, F1, not_93_out);
  and and_14 (and_14_out, not_94_out, not_95_out, not_96_out, not_97_out, not_98_out, not_99_out, F5, not_100_out, not_101_out, F2, not_102_out, not_103_out);
  and and_15 (and_15_out, not_104_out, not_105_out, not_106_out, not_107_out, not_108_out, not_109_out, F5, not_110_out, not_111_out, F2, F1, F0);
  and and_16 (and_16_out, not_112_out, not_113_out, not_114_out, not_115_out, not_116_out, not_117_out, F5, not_118_out, F3, not_119_out, F1, not_120_out);
  and and_17 (and_17_out, not_121_out, not_122_out, OP3, OP2, not_123_out, not_124_out);
  and and_18 (and_18_out, not_125_out, not_126_out, OP3, not_127_out, OP1, not_128_out);
  and and_19 (and_19_out, not_129_out, not_130_out, not_131_out, not_132_out, not_133_out, not_134_out, F5, not_135_out, not_136_out, not_137_out, not_138_out, not_139_out);
  and and_20 (and_20_out, not_140_out, not_141_out, not_142_out, not_143_out, not_144_out, not_145_out, F5, not_146_out, not_147_out, not_148_out, not_149_out, F0);
  and and_21 (and_21_out, not_150_out, not_151_out, not_152_out, not_153_out, not_154_out, not_155_out, F5, not_156_out, not_157_out, not_158_out, F1, not_159_out);
  and and_22 (and_22_out, not_160_out, not_161_out, not_162_out, not_163_out, not_164_out, not_165_out, F5, not_166_out, not_167_out, F2, not_168_out, not_169_out);
  and and_23 (and_23_out, not_170_out, not_171_out, not_172_out, not_173_out, not_174_out, not_175_out, F5, not_176_out, F3, not_177_out, F1, F0);
  and and_24 (and_24_out, not_178_out, not_179_out, OP3, not_180_out, not_181_out, not_182_out);
  and and_25 (and_25_out, not_183_out, not_184_out, OP3, OP2, not_185_out, not_186_out);
  and and_26 (and_26_out, not_187_out, not_188_out, OP3, not_189_out, not_190_out, OP0);
  and and_27 (and_27_out, OP5, not_191_out, not_192_out, not_193_out, OP1, OP0);
  and and_28 (and_28_out, OP5, not_194_out, OP3, not_195_out, OP1, OP0);
  and and_29 (and_29_out, not_196_out, not_197_out, not_198_out, not_199_out, not_200_out, not_201_out, F5, not_202_out, not_203_out, F2, not_204_out, F0);
  and and_30 (and_30_out, not_205_out, not_206_out, not_207_out, not_208_out, not_209_out, not_210_out, F5, not_211_out, not_212_out, F2, F1, F0);
  and and_31 (and_31_out, not_213_out, not_214_out, not_215_out, not_216_out, not_217_out, not_218_out, F5, not_219_out, F3, not_220_out, F1, not_221_out);
  and and_32 (and_32_out, not_222_out, not_223_out, not_224_out, not_225_out, not_226_out, not_227_out, F5, not_228_out, F3, not_229_out, F1, F0);
  and and_33 (and_33_out, not_230_out, not_231_out, OP3, not_232_out, OP1, not_233_out);
  and and_34 (and_34_out, not_234_out, not_235_out, OP3, OP2, not_236_out, OP0);
  or or_1 (S0, and_1_out, and_2_out, and_3_out, and_4_out, and_5_out, and_6_out, and_7_out, and_8_out, and_9_out, and_10_out, and_11_out);
  or or_2 (S1, and_12_out, and_13_out, and_14_out, and_15_out, and_16_out, and_17_out, and_18_out);
  or or_3 (S2, and_19_out, and_20_out, and_21_out, and_22_out, and_23_out, and_24_out, and_25_out, and_26_out, and_27_out, and_28_out);
  or or_4 (S3, and_29_out, and_30_out, and_31_out, and_32_out, and_33_out, and_34_out);
endmodule

// 控制信号生成
module \控制信号自动生成  (
  input  OP0,
  input  OP1,
  input  OP2,
  input  OP3,
  input  OP4,
  input  OP5,
  input  F0,
  input  F1,
  input  F2,
  input  F3,
  input  F4,
  input  F5,
  output MemToReg,
  output MemWrite,
  output ALU_SRC,
  output RegWrite,
  output SysCALL,
  output SignedExt,
  output RegDst,
  output BEQ,
  output BNE,
  output JR,
  output JUMP,
  output JAL
);

  wire and_3_out, and_4_out, and_5_out, and_6_out, and_7_out, and_8_out, and_9_out, and_10_out, and_11_out,
       and_12_out, and_13_out, and_14_out, and_15_out, and_16_out, and_17_out, and_18_out, and_19_out,
       and_20_out, and_21_out, and_22_out, and_23_out, and_24_out, and_25_out, and_26_out, and_27_out,
       and_29_out, and_30_out, and_31_out, and_36_out, and_37_out, and_38_out, not_1_out, not_2_out,
       not_3_out, not_4_out, not_5_out, not_6_out, not_7_out, not_8_out, not_9_out, not_10_out, not_11_out,
       not_12_out, not_13_out, not_14_out, not_15_out, not_16_out, not_17_out, not_18_out, not_19_out,
       not_20_out, not_21_out, not_22_out, not_23_out, not_24_out, not_25_out, not_26_out, not_27_out,
       not_28_out, not_29_out, not_30_out, not_31_out, not_32_out, not_33_out, not_34_out, not_35_out,
       not_36_out, not_37_out, not_38_out, not_39_out, not_40_out, not_41_out, not_42_out, not_43_out,
       not_44_out, not_45_out, not_46_out, not_47_out, not_48_out, not_49_out, not_50_out, not_51_out,
       not_52_out, not_53_out, not_54_out, not_55_out, not_56_out, not_57_out, not_58_out, not_59_out,
       not_60_out, not_61_out, not_62_out, not_63_out, not_64_out, not_65_out, not_66_out, not_67_out,
       not_68_out, not_69_out, not_70_out, not_71_out, not_72_out, not_73_out, not_74_out, not_75_out,
       not_76_out, not_77_out, not_78_out, not_79_out, not_80_out, not_81_out, not_82_out, not_83_out,
       not_84_out, not_85_out, not_86_out, not_87_out, not_88_out, not_89_out, not_90_out, not_91_out,
       not_92_out, not_93_out, not_94_out, not_95_out, not_96_out, not_97_out, not_98_out, not_99_out,
       not_100_out, not_101_out, not_102_out, not_103_out, not_104_out, not_105_out, not_106_out,
       not_107_out, not_108_out, not_109_out, not_110_out, not_111_out, not_112_out, not_113_out,
       not_114_out, not_115_out, not_116_out, not_117_out, not_118_out, not_119_out, not_120_out,
       not_121_out, not_122_out, not_123_out, not_124_out, not_125_out, not_126_out, not_127_out,
       not_128_out, not_129_out, not_130_out, not_131_out, not_132_out, not_133_out, not_134_out,
       not_135_out, not_136_out, not_137_out, not_138_out, not_139_out, not_140_out, not_141_out,
       not_142_out, not_143_out, not_144_out, not_145_out, not_146_out, not_147_out, not_148_out,
       not_149_out, not_150_out, not_151_out, not_152_out, not_153_out, not_154_out, not_155_out,
       not_156_out, not_157_out, not_158_out, not_159_out, not_160_out, not_161_out, not_162_out,
       not_163_out, not_164_out, not_165_out, not_166_out, not_167_out, not_168_out, not_169_out,
       not_170_out, not_171_out, not_172_out, not_173_out, not_174_out, not_175_out, not_176_out,
       not_177_out, not_178_out, not_179_out, not_180_out, not_181_out, not_182_out, not_183_out,
       not_184_out, not_185_out, not_186_out, not_187_out, not_188_out, not_189_out, not_190_out,
       not_191_out, not_192_out, not_193_out, not_194_out, not_195_out, not_196_out, not_197_out,
       not_198_out, not_199_out, not_200_out, not_201_out, not_202_out, not_203_out, not_204_out,
       not_205_out, not_206_out, not_207_out, not_208_out, not_209_out, not_210_out, not_211_out,
       not_212_out, not_213_out, not_214_out, not_215_out, not_216_out, not_217_out, not_218_out,
       not_219_out, not_220_out, not_221_out, not_222_out, not_223_out, not_224_out, not_225_out,
       not_226_out, not_227_out, not_228_out, not_229_out, not_230_out, not_231_out, not_232_out,
       not_233_out, not_234_out, not_235_out, not_236_out, not_237_out, not_238_out;

  not not_1 (not_1_out, OP4);
  not not_2 (not_2_out, OP3);
  not not_3 (not_3_out, OP2);
  not not_4 (not_4_out, OP4);
  not not_5 (not_5_out, OP2);
  not not_6 (not_6_out, OP5);
  not not_7 (not_7_out, OP4);
  not not_8 (not_8_out, OP2);
  not not_9 (not_9_out, OP1);
  not not_10 (not_10_out, OP0);
  not not_11 (not_11_out, OP5);
  not not_12 (not_12_out, OP4);
  not not_13 (not_13_out, OP1);
  not not_14 (not_14_out, OP0);
  not not_15 (not_15_out, OP5);
  not not_16 (not_16_out, OP4);
  not not_17 (not_17_out, OP2);
  not not_18 (not_18_out, OP1);
  not not_19 (not_19_out, OP5);
  not not_20 (not_20_out, OP4);
  not not_21 (not_21_out, OP2);
  not not_22 (not_22_out, OP0);
  not not_23 (not_23_out, OP5);
  not not_24 (not_24_out, OP4);
  not not_25 (not_25_out, OP1);
  not not_26 (not_26_out, OP4);
  not not_27 (not_27_out, OP3);
  not not_28 (not_28_out, OP2);
  not not_29 (not_29_out, OP4);
  not not_30 (not_30_out, OP2);
  not not_31 (not_31_out, OP5);
  not not_32 (not_32_out, OP4);
  not not_33 (not_33_out, OP3);
  not not_34 (not_34_out, OP2);
  not not_35 (not_35_out, OP1);
  not not_36 (not_36_out, OP0);
  not not_37 (not_37_out, F5);
  not not_38 (not_38_out, F4);
  not not_39 (not_39_out, F3);
  not not_40 (not_40_out, F2);
  not not_41 (not_41_out, F1);
  not not_42 (not_42_out, F0);
  not not_43 (not_43_out, OP5);
  not not_44 (not_44_out, OP4);
  not not_45 (not_45_out, OP3);
  not not_46 (not_46_out, OP2);
  not not_47 (not_47_out, OP1);
  not not_48 (not_48_out, OP0);
  not not_49 (not_49_out, F5);
  not not_50 (not_50_out, F4);
  not not_51 (not_51_out, F3);
  not not_52 (not_52_out, F2);
  not not_53 (not_53_out, OP5);
  not not_54 (not_54_out, OP4);
  not not_55 (not_55_out, OP3);
  not not_56 (not_56_out, OP2);
  not not_57 (not_57_out, OP1);
  not not_58 (not_58_out, OP0);
  not not_59 (not_59_out, F5);
  not not_60 (not_60_out, F4);
  not not_61 (not_61_out, F3);
  not not_62 (not_62_out, F2);
  not not_63 (not_63_out, F0);
  not not_64 (not_64_out, OP5);
  not not_65 (not_65_out, OP4);
  not not_66 (not_66_out, OP3);
  not not_67 (not_67_out, OP2);
  not not_68 (not_68_out, OP1);
  not not_69 (not_69_out, OP0);
  not not_70 (not_70_out, F4);
  not not_71 (not_71_out, F3);
  not not_72 (not_72_out, F2);
  not not_73 (not_73_out, F1);
  not not_74 (not_74_out, F0);
  not not_75 (not_75_out, OP5);
  not not_76 (not_76_out, OP4);
  not not_77 (not_77_out, OP3);
  not not_78 (not_78_out, OP2);
  not not_79 (not_79_out, OP1);
  not not_80 (not_80_out, OP0);
  not not_81 (not_81_out, F4);
  not not_82 (not_82_out, F3);
  not not_83 (not_83_out, F2);
  not not_84 (not_84_out, F1);
  not not_85 (not_85_out, OP5);
  not not_86 (not_86_out, OP4);
  not not_87 (not_87_out, OP3);
  not not_88 (not_88_out, OP2);
  not not_89 (not_89_out, OP1);
  not not_90 (not_90_out, OP0);
  not not_91 (not_91_out, F4);
  not not_92 (not_92_out, F3);
  not not_93 (not_93_out, F2);
  not not_94 (not_94_out, F0);
  not not_95 (not_95_out, OP5);
  not not_96 (not_96_out, OP4);
  not not_97 (not_97_out, OP3);
  not not_98 (not_98_out, OP2);
  not not_99 (not_99_out, OP1);
  not not_100 (not_100_out, OP0);
  not not_101 (not_101_out, F4);
  not not_102 (not_102_out, F3);
  not not_103 (not_103_out, F1);
  not not_104 (not_104_out, F0);
  not not_105 (not_105_out, OP5);
  not not_106 (not_106_out, OP4);
  not not_107 (not_107_out, OP3);
  not not_108 (not_108_out, OP2);
  not not_109 (not_109_out, OP1);
  not not_110 (not_110_out, OP0);
  not not_111 (not_111_out, F4);
  not not_112 (not_112_out, F3);
  not not_113 (not_113_out, F1);
  not not_114 (not_114_out, OP5);
  not not_115 (not_115_out, OP4);
  not not_116 (not_116_out, OP3);
  not not_117 (not_117_out, OP2);
  not not_118 (not_118_out, OP1);
  not not_119 (not_119_out, OP0);
  not not_120 (not_120_out, F4);
  not not_121 (not_121_out, F3);
  not not_122 (not_122_out, OP5);
  not not_123 (not_123_out, OP4);
  not not_124 (not_124_out, OP3);
  not not_125 (not_125_out, OP2);
  not not_126 (not_126_out, OP1);
  not not_127 (not_127_out, OP0);
  not not_128 (not_128_out, F4);
  not not_129 (not_129_out, F2);
  not not_130 (not_130_out, F0);
  not not_131 (not_131_out, OP5);
  not not_132 (not_132_out, OP4);
  not not_133 (not_133_out, OP3);
  not not_134 (not_134_out, OP2);
  not not_135 (not_135_out, OP1);
  not not_136 (not_136_out, OP0);
  not not_137 (not_137_out, F4);
  not not_138 (not_138_out, F2);
  not not_139 (not_139_out, OP5);
  not not_140 (not_140_out, OP4);
  not not_141 (not_141_out, OP3);
  not not_142 (not_142_out, OP2);
  not not_143 (not_143_out, OP5);
  not not_144 (not_144_out, OP4);
  not not_145 (not_145_out, OP2);
  not not_146 (not_146_out, OP1);
  not not_147 (not_147_out, OP0);
  not not_148 (not_148_out, OP5);
  not not_149 (not_149_out, OP4);
  not not_150 (not_150_out, OP1);
  not not_151 (not_151_out, OP0);
  not not_152 (not_152_out, OP5);
  not not_153 (not_153_out, OP4);
  not not_154 (not_154_out, OP2);
  not not_155 (not_155_out, OP1);
  not not_156 (not_156_out, OP5);
  not not_157 (not_157_out, OP4);
  not not_158 (not_158_out, OP2);
  not not_159 (not_159_out, OP0);
  not not_160 (not_160_out, OP5);
  not not_161 (not_161_out, OP4);
  not not_162 (not_162_out, OP1);
  not not_163 (not_163_out, OP4);
  not not_164 (not_164_out, OP3);
  not not_165 (not_165_out, OP2);
  not not_166 (not_166_out, OP5);
  not not_167 (not_167_out, OP4);
  not not_168 (not_168_out, OP3);
  not not_169 (not_169_out, OP2);
  not not_170 (not_170_out, OP1);
  not not_171 (not_171_out, OP0);
  not not_172 (not_172_out, F5);
  not not_173 (not_173_out, F4);
  not not_174 (not_174_out, F1);
  not not_175 (not_175_out, F0);
  not not_176 (not_176_out, OP5);
  not not_177 (not_177_out, OP4);
  not not_178 (not_178_out, OP2);
  not not_179 (not_179_out, OP1);
  not not_180 (not_180_out, OP0);
  not not_181 (not_181_out, OP5);
  not not_182 (not_182_out, OP4);
  not not_183 (not_183_out, OP2);
  not not_184 (not_184_out, OP1);
  not not_185 (not_185_out, OP5);
  not not_186 (not_186_out, OP4);
  not not_187 (not_187_out, OP2);
  not not_188 (not_188_out, OP0);
  not not_189 (not_189_out, OP5);
  not not_190 (not_190_out, OP4);
  not not_191 (not_191_out, OP3);
  not not_192 (not_192_out, OP2);
  not not_193 (not_193_out, OP1);
  not not_194 (not_194_out, OP0);
  not not_195 (not_195_out, OP5);
  not not_196 (not_196_out, OP4);
  not not_197 (not_197_out, OP3);
  not not_198 (not_198_out, OP1);
  not not_199 (not_199_out, OP0);
  not not_200 (not_200_out, OP5);
  not not_201 (not_201_out, OP4);
  not not_202 (not_202_out, OP3);
  not not_203 (not_203_out, OP1);
  not not_204 (not_204_out, OP5);
  not not_205 (not_205_out, OP4);
  not not_206 (not_206_out, OP3);
  not not_207 (not_207_out, OP2);
  not not_208 (not_208_out, OP1);
  not not_209 (not_209_out, OP0);
  not not_210 (not_210_out, F5);
  not not_211 (not_211_out, F4);
  not not_212 (not_212_out, F2);
  not not_213 (not_213_out, F1);
  not not_214 (not_214_out, F0);
  not not_215 (not_215_out, OP5);
  not not_216 (not_216_out, OP4);
  not not_217 (not_217_out, OP3);
  not not_218 (not_218_out, OP2);
  not not_219 (not_219_out, OP1);
  not not_220 (not_220_out, OP0);
  not not_221 (not_221_out, F5);
  not not_222 (not_222_out, F4);
  not not_223 (not_223_out, F2);
  not not_224 (not_224_out, F1);
  not not_225 (not_225_out, F0);
  not not_226 (not_226_out, OP5);
  not not_227 (not_227_out, OP4);
  not not_228 (not_228_out, OP3);
  not not_229 (not_229_out, OP2);
  not not_230 (not_230_out, OP0);
  not not_231 (not_231_out, OP5);
  not not_232 (not_232_out, OP4);
  not not_233 (not_233_out, OP3);
  not not_234 (not_234_out, OP2);
  not not_235 (not_235_out, OP5);
  not not_236 (not_236_out, OP4);
  not not_237 (not_237_out, OP3);
  not not_238 (not_238_out, OP2);
  and and_1 (MemToReg, OP5, not_1_out, not_2_out, not_3_out, OP1, OP0);
  and and_2 (MemWrite, OP5, not_4_out, OP3, not_5_out, OP1, OP0);
  and and_3 (and_3_out, not_6_out, not_7_out, OP3, not_8_out, not_9_out, not_10_out);
  and and_4 (and_4_out, not_11_out, not_12_out, OP3, OP2, not_13_out, not_14_out);
  and and_5 (and_5_out, not_15_out, not_16_out, OP3, not_17_out, not_18_out, OP0);
  and and_6 (and_6_out, not_19_out, not_20_out, OP3, not_21_out, OP1, not_22_out);
  and and_7 (and_7_out, not_23_out, not_24_out, OP3, OP2, not_25_out, OP0);
  and and_8 (and_8_out, OP5, not_26_out, not_27_out, not_28_out, OP1, OP0);
  and and_9 (and_9_out, OP5, not_29_out, OP3, not_30_out, OP1, OP0);
  and and_10 (and_10_out, not_31_out, not_32_out, not_33_out, not_34_out, not_35_out, not_36_out, not_37_out, not_38_out, not_39_out, not_40_out, not_41_out, not_42_out);
  and and_11 (and_11_out, not_43_out, not_44_out, not_45_out, not_46_out, not_47_out, not_48_out, not_49_out, not_50_out, not_51_out, not_52_out, F1, F0);
  and and_12 (and_12_out, not_53_out, not_54_out, not_55_out, not_56_out, not_57_out, not_58_out, not_59_out, not_60_out, not_61_out, not_62_out, F1, not_63_out);
  and and_13 (and_13_out, not_64_out, not_65_out, not_66_out, not_67_out, not_68_out, not_69_out, F5, not_70_out, not_71_out, not_72_out, not_73_out, not_74_out);
  and and_14 (and_14_out, not_75_out, not_76_out, not_77_out, not_78_out, not_79_out, not_80_out, F5, not_81_out, not_82_out, not_83_out, not_84_out, F0);
  and and_15 (and_15_out, not_85_out, not_86_out, not_87_out, not_88_out, not_89_out, not_90_out, F5, not_91_out, not_92_out, not_93_out, F1, not_94_out);
  and and_16 (and_16_out, not_95_out, not_96_out, not_97_out, not_98_out, not_99_out, not_100_out, F5, not_101_out, not_102_out, F2, not_103_out, not_104_out);
  and and_17 (and_17_out, not_105_out, not_106_out, not_107_out, not_108_out, not_109_out, not_110_out, F5, not_111_out, not_112_out, F2, not_113_out, F0);
  and and_18 (and_18_out, not_114_out, not_115_out, not_116_out, not_117_out, not_118_out, not_119_out, F5, not_120_out, not_121_out, F2, F1, F0);
  and and_19 (and_19_out, not_122_out, not_123_out, not_124_out, not_125_out, not_126_out, not_127_out, F5, not_128_out, F3, not_129_out, F1, not_130_out);
  and and_20 (and_20_out, not_131_out, not_132_out, not_133_out, not_134_out, not_135_out, not_136_out, F5, not_137_out, F3, not_138_out, F1, F0);
  and and_21 (and_21_out, not_139_out, not_140_out, not_141_out, not_142_out, OP1, OP0);
  and and_22 (and_22_out, not_143_out, not_144_out, OP3, not_145_out, not_146_out, not_147_out);
  and and_23 (and_23_out, not_148_out, not_149_out, OP3, OP2, not_150_out, not_151_out);
  and and_24 (and_24_out, not_152_out, not_153_out, OP3, not_154_out, not_155_out, OP0);
  and and_25 (and_25_out, not_156_out, not_157_out, OP3, not_158_out, OP1, not_159_out);
  and and_26 (and_26_out, not_160_out, not_161_out, OP3, OP2, not_162_out, OP0);
  and and_27 (and_27_out, OP5, not_163_out, not_164_out, not_165_out, OP1, OP0);
  and and_28 (SysCALL, not_166_out, not_167_out, not_168_out, not_169_out, not_170_out, not_171_out, not_172_out, not_173_out, F3, F2, not_174_out, not_175_out);
  and and_29 (and_29_out, not_176_out, not_177_out, OP3, not_178_out, not_179_out, not_180_out);
  and and_30 (and_30_out, not_181_out, not_182_out, OP3, not_183_out, not_184_out, OP0);
  and and_31 (and_31_out, not_185_out, not_186_out, OP3, not_187_out, OP1, not_188_out);
  and and_32 (RegDst, not_189_out, not_190_out, not_191_out, not_192_out, not_193_out, not_194_out);
  and and_33 (BEQ, not_195_out, not_196_out, not_197_out, OP2, not_198_out, not_199_out);
  and and_34 (BNE, not_200_out, not_201_out, not_202_out, OP2, not_203_out, OP0);
  and and_35 (JR, not_204_out, not_205_out, not_206_out, not_207_out, not_208_out, not_209_out, not_210_out, not_211_out, F3, not_212_out, not_213_out, not_214_out);
  and and_36 (and_36_out, not_215_out, not_216_out, not_217_out, not_218_out, not_219_out, not_220_out, not_221_out, not_222_out, F3, not_223_out, not_224_out, not_225_out);
  and and_37 (and_37_out, not_226_out, not_227_out, not_228_out, not_229_out, OP1, not_230_out);
  and and_38 (and_38_out, not_231_out, not_232_out, not_233_out, not_234_out, OP1, OP0);
  and and_39 (JAL, not_235_out, not_236_out, not_237_out, not_238_out, OP1, OP0);
  or or_1 (ALU_SRC, and_3_out, and_4_out, and_5_out, and_6_out, and_7_out, and_8_out, and_9_out);
  or or_2 (SignedExt, and_29_out, and_30_out, and_31_out);
  or or_3 (JUMP, and_36_out, and_37_out, and_38_out);
  or or_4 (RegWrite, and_10_out, and_11_out, and_12_out, and_13_out, and_14_out, and_15_out, and_16_out, and_17_out, and_18_out, and_19_out, and_20_out, and_21_out, and_22_out, and_23_out, and_24_out, and_25_out, and_26_out, and_27_out);
endmodule

// ALU
module MIPS_ALU (
  input  [4:0] shamt,
  input  [31:0] X,
  input  [31:0] Y,
  input  [3:0] AluOP,
  output Equal,
  output [31:0] Result,
  output [31:0] Result_2
);

  wire [0:0] comparator_1_lt, comparator_2_lt;
  wire [31:0] adder_1_out, AND_out, divider_1_out, divider_1_rem, multiplier_1_cout, multiplier_1_out,
       NOR_out, OR_out, shifter_1_out, shifter_2_out, shifter_3_out, subtractor_1_out, XOR_out;

  assign AND_out = X & Y;  // AND_Gate AND, 32 bits wide
  assign OR_out = X | Y;  // OR_Gate OR, 32 bits wide
  Shifter #(.width(32)) shifter_1 (.in(Y), .\dist (shamt), .out(shifter_1_out));
  Shifter #(.width(32), .shift("ar")) shifter_2 (.in(Y), .\dist (shamt), .out(shifter_2_out));
  Shifter #(.width(32), .shift("lr")) shifter_3 (.in(Y), .\dist (shamt), .out(shifter_3_out));
  Multiplier #(.width(32)) multiplier_1 (.a(X), .b(Y), .out(multiplier_1_out), .cout(multiplier_1_cout));  // open: cin
  Divider #(.width(32)) divider_1 (.a(X), .b(Y), .out(divider_1_out), .rem(divider_1_rem));  // open: upper
  Adder #(.width(32)) adder_1 (.a(X), .b(Y), .out(adder_1_out));  // open: cin, cout
  Subtractor #(.width(32)) subtractor_1 (.a(X), .b(Y), .out(subtractor_1_out));  // open: bin, bout
  assign XOR_out = X ^ Y;  // XOR_Gate XOR, 32 bits wide
  assign NOR_out = ~(X | Y);  // NOR_Gate NOR, 32 bits wide
  Comparator #(.width(32)) comparator_1 (.a(X), .b(Y), .eq(Equal), .lt(comparator_1_lt[0]));  // open: gt
  Comparator #(.width(32), .mode("unsigned")) comparator_2 (.a(X), .b(Y), .lt(comparator_2_lt[0]));  // open: gt, eq
  Multiplexer #(.select(4), .width(32), .enable("false")) multiplexer_1 (
    .in0(shifter_1_out), .in1(shifter_2_out), .in2(shifter_3_out), .in3(multiplier_1_out),
    .in4(divider_1_out), .in5(adder_1_out), .in6(subtractor_1_out), .in7(AND_out), .in8(OR_out),
    .in9(XOR_out), .in10(NOR_out), .in11({{31{1'b0}}, comparator_1_lt[0]}),
    .in12({{31{1'b0}}, comparator_2_lt[0]}), .in13({32{1'b0}}), .in14({32{1'b0}}), .in15({32{1'b0}}),
    .out(Result), .sel(AluOP));
  Multiplexer #(.select(4), .width(32), .enable("false")) multiplexer_2 (
    .in0({32{1'b0}}), .in1({32{1'b0}}), .in2({32{1'b0}}), .in3(multiplier_1_cout), .in4(divider_1_rem),
    .in5({32{1'b0}}), .in6({32{1'b0}}), .in7({32{1'b0}}), .in8({32{1'b0}}), .in9({32{1'b0}}),
    .in10({32{1'b0}}), .in11({32{1'b0}}), .in12({32{1'b0}}), .in13({32{1'b0}}), .in14({32{1'b0}}),
    .in15({32{1'b0}}), .out(Result_2), .sel(AluOP));

  // Other names for the same wires on the sheet: Result2[31:0] = Result_2; S[3:0] = AluOP

  // Notes on the sheet:
  //   不要改变此引脚区域内容，也不要改变ALU封装形式
  //   输入引脚
  //   输出引脚
endmodule

module MIPS_Regifile (
  input  [31:0] Din,
  input  Clk,
  input  WE,
  input  [4:0] R1_num,
  input  [4:0] W_num,
  input  [4:0] R2_num,
  output [31:0] R1,
  output [31:0] R2
);

  // RegisterFile registerfile_1: pin names not known; wires that end beside it: Din, Clk, WE, W_num, R1_num, R2_num, R1, R2
endmodule
